// Digital circuit atividade-3-exercicio-2-item-b.dig as structural Verilog
module atividade_3_exercicio_2_item_b (
  input  A,
  input  B,
  input  C,
  input  D,
  input  E,
  output S1,
  output S0
);

  wire and_1_out, and_2_out, and_3_out, nand_1_out, nor_1_out, nor_2_out, not_1_out, not_2_out, xnor_1_out;

  not not_1 (not_1_out, B);
  not not_2 (not_2_out, D);
  nand nand_1 (nand_1_out, not_1_out, A, C);
  nor nor_1 (nor_1_out, not_2_out, C);
  xnor xnor_1 (xnor_1_out, nand_1_out, D);
  nor nor_2 (nor_2_out, A, C, E);
  and and_1 (and_1_out, nand_1_out, A);
  and and_2 (and_2_out, xnor_1_out, nor_2_out);
  and and_3 (and_3_out, B, E);
  nor nor_3 (S1, and_2_out, and_3_out);
  or or_1 (S0, and_1_out, nor_1_out);
endmodule
