// Digital circuit circuitos-logicos-combinatoriais.dig as structural Verilog
module circuitos_logicos_combinatoriais (
  input  A,
  input  B,
  input  C,
  input  A_2,
  input  B_2,
  input  C_2,
  input  A_3,
  input  B_3,
  input  C_3,
  input  D,
  output S,
  output S_2,
  output S_3
);

  wire and_1_out, and_2_out, nand_1_out, nand_2_out, or_1_out, xnor_1_out;

  and and_1 (and_1_out, C, B);
  nand nand_1 (nand_1_out, C, A);
  or or_1 (or_1_out, C_3, B_3);
  xnor xnor_1 (xnor_1_out, D, A_3);
  or or_2 (S, and_1_out, nand_1_out);
  xor xor_1 (S_3, or_1_out, xnor_1_out);
  and and_2 (and_2_out, C_2, ~B_2);  // And
  nand nand_2 (nand_2_out, C_2, A_2);
  xor xor_2 (S_2, and_2_out, nand_2_out);

  // Notes on the sheet:
  //   S = (B + C)  (
  //   (C ∨ B) ∧ (A ∨ C) ∧ (B ∨ !C) * (C + !A)
  //   S = BC + ~AC
  //   S = BC + ~A~C
  //   S = ~BC~ + AC
  //   S = BC xor ~AC
  //   A = 1
  //   B = 0
  //   C = 1
endmodule
