// Digital circuit Circ#2-S2-ieee.dig as structural Verilog
module Circ_2_S2_ieee (
  input  A0,
  input  A1,
  input  A2,
  input  A3,
  output Y
);

  wire and_1_out, and_2_out, and_3_out, not_1_out, not_2_out, or_1_out;

  not not_1 (not_1_out, A0);
  not not_2 (not_2_out, A1);
  and and_1 (and_1_out, not_1_out, A1);
  and and_2 (and_2_out, A0, not_2_out);
  and and_3 (and_3_out, and_2_out, A3);
  or or_1 (or_1_out, and_1_out, and_3_out);
  or or_2 (Y, or_1_out, A2);
endmodule
