// Digital circuit Circ#7-S2-ieee.dig as structural Verilog
module Circ_7_S2_ieee (
  input  A0,
  input  A1,
  input  A2,
  input  A3,
  output Y
);

  wire and_1_out, and_2_out, and_3_out, and_4_out, and_5_out, and_6_out, not_1_out, not_2_out, not_3_out,
       not_4_out, or_1_out, or_2_out;

  not not_1 (not_1_out, A0);
  not not_2 (not_2_out, A1);
  not not_3 (not_3_out, A2);
  not not_4 (not_4_out, A3);
  and and_1 (and_1_out, not_1_out, not_3_out);
  and and_2 (and_2_out, not_1_out, not_4_out);
  and and_3 (and_3_out, A0, A1);
  and and_4 (and_4_out, not_2_out, A2);
  or or_1 (or_1_out, and_1_out, and_2_out);
  and and_5 (and_5_out, and_3_out, A3);
  and and_6 (and_6_out, and_4_out, not_4_out);
  or or_2 (or_2_out, and_5_out, and_6_out);
  or or_3 (Y, or_1_out, or_2_out);
endmodule
