// Logisim project circuitos-digitais-2.circ as structural Verilog
module cont_sinc_3_bits_exemplo_combinatorio (
  input  nQ2,
  input  nQ1,
  input  nQ0,
  input  Q2,
  input  Q1,
  input  Q0,
  output D2,
  output D1,
  output D0
);

  wire and_1_out, and_2_out, and_3_out, and_4_out, and_5_out, and_6_out, and_7_out, or_2_out;

  and and_1 (and_1_out, nQ2, nQ1);
  or or_1 (D2, and_1_out, and_2_out);
  and and_2 (and_2_out, nQ2, nQ0);
  and and_3 (and_3_out, nQ2, nQ0);
  or or_2 (or_2_out, and_3_out, and_4_out);
  and and_4 (and_4_out, nQ1, nQ0);
  and and_5 (and_5_out, Q1, Q0);
  and and_6 (and_6_out, nQ1, nQ0);
  or or_3 (D0, and_6_out, and_7_out);
  and and_7 (and_7_out, Q2, Q1);
  or or_4 (D1, or_2_out, and_5_out);
endmodule
