// Logisim project 028 - cronometro-inicia-para-marca-zera.circ as structural Verilog: 3 circuits, main circuit main
module main (
);

  wire and_1_out, and_2_out, B1_out, B2_out, Gerador_de_Pulsos_out, \Ini_Pára_q , Marca_q, Marca_qn,
       not_1_out, or_1_out, POR_out, Zera_q;
  wire [3:0] Contador_q, Latch_q;

  Clock Gerador_de_Pulsos (.out(Gerador_de_Pulsos_out));
  Button B1 (.out(B1_out));
  Button B2 (.out(B2_out));
  Button POR (.out(POR_out));
  // Probe on POR_out
  T_Flip_Flop #(.trigger("falling")) \Ini_Pára  (
    .clk(B1_out), .T(1'b1), .Q(\Ini_Pára_q ), .reset(POR_out));  // open: Qn, preset, en
  or or_1 (or_1_out, \Ini_Pára_q , Marca_qn);
  and and_1 (and_1_out, Gerador_de_Pulsos_out, \Ini_Pára_q );
  D_Flip_Flop #(.trigger("falling")) Zera (
    .clk(B2_out), .D(not_1_out), .Q(Zera_q), .preset(POR_out), .reset(and_2_out));  // open: Qn, en
  not not_1 (not_1_out, or_1_out);
  and and_2 (and_2_out, Zera_q, ~POR_out);  // AND_Gate
  Counter #(.width(4), .max('hf), .trigger("falling")) Contador (
    .Q(Contador_q), .clk(and_1_out), .clr(Zera_q));  // open: load, D, count, carry
  Register #(.width(4), .trigger("high")) Latch (.D(Contador_q), .Q(Latch_q), .clk(Marca_q));  // open: en, clr
  T_Flip_Flop #(.trigger("falling")) Marca (
    .clk(B2_out), .T(or_1_out), .Q(Marca_q), .Qn(Marca_qn), .preset(POR_out));  // open: reset, en
  Hex_Digit_Display hex_digit_display_1 (.value(Latch_q));  // open: dp
endmodule

// Cronômetro
module cronometro (
  input  ck,
  input  iniciar_parar,
  input  marcar_zerar,
  input  limpar,
  output [3:0] saidas
);

  wire and_1_out, and_2_out, \Ini_Pára_q , Marca_q, Marca_qn, not_1_out, or_1_out, Zera_q;
  wire [3:0] Contador_q;

  T_Flip_Flop #(.trigger("falling")) \Ini_Pára  (
    .clk(iniciar_parar), .T(1'b1), .Q(\Ini_Pára_q ), .reset(limpar));  // open: Qn, preset, en
  and and_1 (and_1_out, ck, \Ini_Pára_q );
  or or_1 (or_1_out, \Ini_Pára_q , Marca_qn);
  not not_1 (not_1_out, or_1_out);
  Counter #(.width(4), .max('hf), .trigger("falling")) Contador (
    .Q(Contador_q), .clk(and_1_out), .clr(Zera_q));  // open: load, D, count, carry
  D_Flip_Flop #(.trigger("falling")) Zera (
    .clk(marcar_zerar), .D(not_1_out), .Q(Zera_q), .preset(limpar), .reset(and_2_out));  // open: Qn, en
  and and_2 (and_2_out, Zera_q, ~limpar);  // AND_Gate
  Register #(.width(4), .trigger("high")) Latch (.D(Contador_q), .Q(saidas), .clk(Marca_q));  // open: en, clr
  T_Flip_Flop #(.trigger("falling")) Marca (
    .clk(marcar_zerar), .T(or_1_out), .Q(Marca_q), .Qn(Marca_qn), .preset(limpar));  // open: reset, en
endmodule

module uso_cronometro (
);

  wire B1_out, B2_out, Gerador_de_Pulsos_out, POR_out;
  wire [3:0] cronometro_1_saidas;

  Clock Gerador_de_Pulsos (.out(Gerador_de_Pulsos_out));
  Button B1 (.out(B1_out));
  Button B2 (.out(B2_out));
  Button POR (.out(POR_out));
  cronometro cronometro_1 (
    .ck(Gerador_de_Pulsos_out), .iniciar_parar(B1_out), .marcar_zerar(B2_out), .limpar(POR_out),
    .saidas(cronometro_1_saidas));
  Hex_Digit_Display hex_digit_display_1 (.value(cronometro_1_saidas));  // open: dp

  // Notes on the sheet:
  //   Mostrador
endmodule
