// Logisim project senha-cadeado.circ as structural Verilog: 1 circuit, main circuit main
module main (
  input  in_1,
  input  in_2,
  input  in_3
);

  wire and_1_out, and_2_out, button_1_out, button_2_out, d_ff_1_q, d_ff_2_q, not_1_out, not_2_out;

  not not_1 (not_1_out, in_3);
  not not_2 (not_2_out, in_2);
  and and_1 (and_1_out, d_ff_1_q, in_1, in_2, not_1_out);
  and and_2 (and_2_out, in_1, not_2_out, in_3);
  Button button_1 (.out(button_1_out));
  D_Flip_Flop d_ff_1 (
    .clk(button_1_out), .D(and_2_out), .Q(d_ff_1_q), .en(1'b1), .reset(button_2_out));  // open: Qn, preset
  LED led_1 (.in(d_ff_2_q));
  D_Flip_Flop d_ff_2 (
    .clk(button_1_out), .D(and_1_out), .Q(d_ff_2_q), .en(1'b1), .reset(button_2_out));  // open: Qn, preset
  Button button_2 (.out(button_2_out));
endmodule
