// Logisim project comparador.circ as structural Verilog: 3 circuits, main circuit main
module main (
);

  wire and_1_out, or_1_out, or_2_out, undriven, undriven_2, undriven_3;

  or or_1 (or_1_out, undriven, undriven_2);
  or or_2 (or_2_out, and_1_out, or_1_out);
  and and_1 (and_1_out, or_2_out, undriven_3);
endmodule

module Comparador_XNOR (
  input  A3,
  input  B3,
  input  A2,
  input  B2,
  input  A1,
  input  B1,
  input  A0,
  input  B0,
  output [3:0] out_9,
  output [3:0] out_10
);

  wire and_1_out, and_2_out, and_3_out, xnor_1_out, xnor_2_out, xnor_3_out, xnor_4_out;

  xnor xnor_1 (xnor_1_out, A3, B3);
  xnor xnor_2 (xnor_2_out, A2, B2);
  xnor xnor_3 (xnor_3_out, A1, B1);
  xnor xnor_4 (xnor_4_out, A0, B0);
  and and_1 (and_1_out, xnor_1_out, xnor_2_out);
  and and_2 (and_2_out, xnor_3_out, xnor_4_out);
  and and_3 (and_3_out, and_1_out, and_2_out);
  LED led_1 (.in(and_3_out));

  assign out_9 = {A3, A2, A1, A0};
  assign out_10 = {B3, B2, B1, B0};
endmodule

module Comparador_XOR (
  input  A3,
  input  B3,
  input  A2,
  input  B2,
  input  A1,
  input  B1,
  input  A0,
  input  B0,
  output [3:0] out_9,
  output [3:0] out_10
);

  wire nor_1_out, or_1_out, or_2_out, xor_1_out, xor_2_out, xor_3_out, xor_4_out;

  xor xor_1 (xor_1_out, A3, B3);
  xor xor_2 (xor_2_out, A2, B2);
  xor xor_3 (xor_3_out, A1, B1);
  xor xor_4 (xor_4_out, A0, B0);
  or or_1 (or_1_out, xor_1_out, xor_2_out);
  or or_2 (or_2_out, xor_3_out, xor_4_out);
  nor nor_1 (nor_1_out, or_1_out, or_2_out);
  LED led_1 (.in(nor_1_out));

  assign out_9 = {A3, A2, A1, A0};
  assign out_10 = {B3, B2, B1, B0};
endmodule
