// Digital circuit ff-rs.dig as structural Verilog
module ff_rs (
  input  R,
  input  S,
  output Q,
  output nQ
);

  wire switchdt_1_p3;

  // SwitchDT switchdt_1: pin names not known; wires that end beside it: R, S, switchdt_1_p3
  nand nand_1 (Q, R, nQ);
  nand nand_2 (nQ, Q, switchdt_1_p3);
endmodule
