// Digital circuit apresentacao.dig as structural Verilog
module apresentacao (
);

  flip_flop_d_ck0 flip_flop_d_ck0_1 ();  // open: ck, D, Q, nQ
  flip_flop_d_s0_r0_ck0_contador_1bit flip_flop_d_s0_r0_ck0_contador_1bit_1 ();  // open: nS, nR, ck, Q, nQ
  flip_flop_d_s0_r0_ck0_contador_4bits flip_flop_d_s0_r0_ck0_contador_4bits_1 ();  // open: nMS, nMR, ck, Q0, Q1, Q2, Q3
  flip_flop_d_s0_r0_ck1_contador_4bits flip_flop_d_s0_r0_ck1_contador_4bits_1 ();  // open: nMS, nMR, ck, Q0, Q1, Q2, Q3
  // _7474 _7474_1: pin names not known
  tinkercad_contador_assincrono_detalhes tinkercad_contador_assincrono_detalhes_1 ();
  tinkercad_contador_assincrono_com_pinagem tinkercad_contador_assincrono_com_pinagem_1 ();
  // _7474 _7474_2: pin names not known
  flip_flop_d_s0_r0_ck1_contador_crescente_0_a_9_4bits flip_flop_d_s0_r0_ck1_contador_crescente_0_a_9_4bits_1 ();  // open: nMS, ck, nMR, Q0, Q1, Q2, Q3
  flip_flop_d_ck0_contador_1bit flip_flop_d_ck0_contador_1bit_1 ();  // open: ck, Q, nQ
  flip_flop_d_s0_r0_ck0_contador_2bits flip_flop_d_s0_r0_ck0_contador_2bits_1 ();  // open: nS, nR, ck, Q0, Q1
  flip_flop_d_s0_r0_ck1_contador_crescente_4bits flip_flop_d_s0_r0_ck1_contador_crescente_4bits_1 ();  // open: nMS, nMR, ck, Q0, Q1, Q2, Q3

  // Notes on the sheet:
  //   _ 1) Na montagem "ETE102-Contador_Assíncrono_0_a_9", por que o MS' "não funciona"? Ou seja,
  //          por que, ao soltá-lo, todos os LEDs não ficam em 1?
  //   _ 2) Que alterações seriam necessárias no circuito para que, após aplicar MS', tenha-se o
  //          número 9 (1001)?
  //   _ 3) Implementar um contador assíncrono crescente de 0 a 9 utilizando o CI 74HC93.
  //   1) Implementar um contador crescente/decrescente de 0 a 15.
  //   2) Implementar um contador crescente/decrescente *automático* de 0 a 15.
  //       Ou seja, na contagem crescente, após atingir o 15, inicia-se a contagem decrescente
  //       e, após atingir o zero, inicia-se novamente a contagem crescente.
  //   3) Alterar o circuito anterior para implementar um contador crescente/decrescente
  //       *automático* de 0 a 9.
  //   Contador
  //   _   ETE102-Contador_Assíncrono
  //   Questão
  //   Quando ocorre o incremento da contagem?
  //     1) Ao soltar o botão ck, produzindo uma borda de descida.
  //     2) Ao pressionar o botão ck, produzindo uma borda de subida.
  //     3) Ao soltar o botão ck, produzindo uma borda de subida.
  //     4) Ao pressionar o botão ck, produzindo uma borda de descida.
  //     5) Somente ao pressionar e soltar o ~MR antes de se pressionar e soltar o ck.
  //   _   ETE102-Contador_Assíncrono_0_a_9
  //   Q_m a Q_n
  //   ~MR
  //   74HC74
  //   CONTADOR ASSÍNCRONO
  //   __ http://pdf.datasheetcatalog.com/datasheet/on_semiconductor2/74HC74.PDF __
  //   Tinkercad
  //   ******************************************
  //   Considerações sobre esquema elétrico
  //   e implementação física.
  //   ******************************************
  //   CONTADOR ASSÍNCRONO DE 0 A 9
  //   ENTREGAS
  //   OPCIONAIS PARA EXERCITAR A IMAGINAÇÃO
  //   (não é necessário entregar)
  //   CLC (Circ. Lóg. Comb.)
  //   E_m a E_n
  //   S
endmodule
