// Digital circuit contador-assincrono.dig as structural Verilog
module contador_assincrono (
  input  ck,
  input  nMR,
  output Q0,
  output Q1,
  output Q2,
  output Q3,
  output [3:0] Q0_Q4
);

  wire d_ff_as_1_nq, d_ff_as_2_nq, d_ff_as_3_nq, d_ff_as_4_nq, nand_1_out, nand_2_out, nand_3_out;

  D_FF_AS d_ff_as_1 (.Set(~1'b1), .D(d_ff_as_1_nq), .C(~ck), .Clr(~nand_2_out), .Q(Q0), .nQ(d_ff_as_1_nq));
  nand nand_1 (nand_1_out, nand_3_out, nMR);
  // Probe on {Q0_Q4[3:1], Q0}
  nand nand_2 (nand_2_out, nand_1_out, nand_1_out);
  D_FF_AS d_ff_as_2 (.Set(~1'b1), .D(d_ff_as_2_nq), .C(~Q0), .Clr(~nand_2_out), .Q(Q0_Q4[1]), .nQ(d_ff_as_2_nq));
  D_FF_AS d_ff_as_3 (.Set(~1'b1), .D(d_ff_as_3_nq), .C(~Q0_Q4[1]), .Clr(~nand_2_out), .Q(Q0_Q4[2]), .nQ(d_ff_as_3_nq));
  D_FF_AS d_ff_as_4 (.Set(~1'b1), .D(d_ff_as_4_nq), .C(~Q0_Q4[2]), .Clr(~nand_2_out), .Q(Q0_Q4[3]), .nQ(d_ff_as_4_nq));
  nand nand_3 (nand_3_out, Q0_Q4[1], Q0_Q4[3]);

  assign Q0_Q4[0] = Q0;
  assign Q1 = Q0_Q4[1];
  assign Q2 = Q0_Q4[2];
  assign Q3 = Q0_Q4[3];
endmodule
