// Digital circuit contador-crescente-decrescente-4bits.dig as structural Verilog
module contador_crescente_decrescente_4bits (
  input  nMR,
  input  ck,
  input  nD_C,
  input  nMS,
  output Q0,
  output Q1,
  output Q2,
  output Q3
);

  wire d_ff_as_1_nq, d_ff_as_2_nq, d_ff_as_3_nq, d_ff_as_4_nq, xor_1_out, xor_2_out, xor_3_out;

  D_FF_AS d_ff_as_1 (.Set(~nMS), .D(d_ff_as_1_nq), .C(ck), .Clr(~nMR), .Q(Q0), .nQ(d_ff_as_1_nq));
  xor xor_1 (xor_1_out, Q0, nD_C);
  D_FF_AS d_ff_as_2 (.Set(~nMS), .D(d_ff_as_2_nq), .C(xor_1_out), .Clr(~nMR), .Q(Q1), .nQ(d_ff_as_2_nq));
  xor xor_2 (xor_2_out, Q1, nD_C);
  D_FF_AS d_ff_as_3 (.Set(~nMS), .D(d_ff_as_3_nq), .C(xor_2_out), .Clr(~nMR), .Q(Q2), .nQ(d_ff_as_3_nq));
  // Probe on {Q3, Q2, Q1, Q0}
  xor xor_3 (xor_3_out, Q2, nD_C);
  D_FF_AS d_ff_as_4 (.Set(~nMS), .D(d_ff_as_4_nq), .C(xor_3_out), .Clr(~nMR), .Q(Q3), .nQ(d_ff_as_4_nq));
  Seven_Seg_Hex seven_seg_hex_1 (.d({Q3, Q2, Q1, Q0}), .dp(1'b0));

  // Notes on the sheet:
  //   nMR: default 1
  //   nD_C: default 1
  //   nMS: default 1
  //   Contador crescente/decrescente
  //   com incremento em borda de subida!
endmodule
