// Digital circuit flip-flop-d-ck0-contador-1bit.dig as structural Verilog
module flip_flop_d_ck0_contador_1bit (
  input  ck,
  output Q,
  output nQ
);

  D_FF d_ff_1 (.D(nQ), .C(~ck), .Q(Q), .nQ(nQ));
  // Probe on Q
  // Probe on nQ
endmodule
