// Digital circuit flip-flop-d-ck0.dig as structural Verilog
module flip_flop_d_ck0 (
  input  ck,
  input  D,
  output Q,
  output nQ
);

  D_FF d_ff_1 (.D(D), .C(~ck), .Q(Q), .nQ(nQ));
  // Probe on Q
  // Probe on nQ
endmodule
