// Digital circuit flip-flop-d-s0-r0-ck0-contador-1bit.dig as structural Verilog
module flip_flop_d_s0_r0_ck0_contador_1bit (
  input  nS,
  input  nR,
  input  ck,
  output Q,
  output nQ
);

  D_FF_AS d_ff_as_1 (.Set(~nS), .D(nQ), .C(~ck), .Clr(~nR), .Q(Q), .nQ(nQ));

  // Notes on the sheet:
  //   nS: default 1
  //   nR: default 1
  //   Se ~S = 0 => Q = 1
  //   Se ~R = 0 => Q = 0
endmodule
