// Digital circuit flip-flop-d-s0-r0-ck0-contador-2bits.dig as structural Verilog
module flip_flop_d_s0_r0_ck0_contador_2bits (
  input  nS,
  input  nR,
  input  ck,
  output Q0,
  output Q1
);

  wire d_ff_as_1_nq, d_ff_as_2_nq;

  D_FF_AS d_ff_as_1 (.Set(~nS), .D(d_ff_as_1_nq), .C(~ck), .Clr(~nR), .Q(Q0), .nQ(d_ff_as_1_nq));
  D_FF_AS d_ff_as_2 (.D(d_ff_as_2_nq), .Q(Q1), .nQ(d_ff_as_2_nq));  // open: Set, C, Clr
  Seven_Seg_Hex seven_seg_hex_1 (.d({2'b00, Q1, Q0}), .dp(1'b0));
  // Probe on {Q1, Q0}

  // Notes on the sheet:
  //   nS: default 1
  //   nR: default 1
  //   ~S passa a ser ~MS
  //   ~R passa a ser ~MR
endmodule
