// Digital circuit flip-flop-d-s0-r0-ck1-contador-crescente-4bits.dig as structural Verilog
module flip_flop_d_s0_r0_ck1_contador_crescente_4bits (
  input  nMS,
  input  nMR,
  input  ck,
  output Q0,
  output Q1,
  output Q2,
  output Q3
);

  wire d_ff_as_1_nq, d_ff_as_2_nq, d_ff_as_3_nq, d_ff_as_4_nq;

  D_FF_AS d_ff_as_1 (.Set(~nMS), .D(d_ff_as_1_nq), .C(ck), .Clr(~nMR), .Q(Q0), .nQ(d_ff_as_1_nq));
  D_FF_AS d_ff_as_2 (.Set(~nMS), .D(d_ff_as_2_nq), .C(d_ff_as_1_nq), .Clr(~nMR), .Q(Q1), .nQ(d_ff_as_2_nq));
  D_FF_AS d_ff_as_3 (.Set(~nMS), .D(d_ff_as_3_nq), .C(d_ff_as_2_nq), .Clr(~nMR), .Q(Q2), .nQ(d_ff_as_3_nq));
  // Probe on {Q3, Q2, Q1, Q0}
  D_FF_AS d_ff_as_4 (.Set(~nMS), .D(d_ff_as_4_nq), .C(d_ff_as_3_nq), .Clr(~nMR), .Q(Q3), .nQ(d_ff_as_4_nq));
  Seven_Seg_Hex seven_seg_hex_1 (.d({Q3, Q2, Q1, Q0}), .dp(1'b0));

  // Notes on the sheet:
  //   nMS: default 1
  //   nMR: default 1
  //   Contador crescente com
  //   incremento em borda de subida!
endmodule
