// Digital circuit tinkercad-contador-assincrono-com-pinagem.dig as structural Verilog
module tinkercad_contador_assincrono_com_pinagem (
);

  wire _7474_1_pin2, _7474_1_pin8, _7474_1_pin9, _7474_2_pin2, _7474_2_pin8, _7474_2_pin9, ck, d_ff_as_1_nq,
       d_ff_as_1_q, d_ff_as_2_nq, d_ff_as_2_q, d_ff_as_3_nq, d_ff_as_3_q, d_ff_as_4_nq, d_ff_as_4_q, nMR,
       nMS, pullup_3_out, pullup_4_out, pullup_6_out, Q0_p1, Q2_p1;

  PullUp pullup_1 (.out(ck));
  PullUp pullup_2 (.out(nMS));
  Switch u_ck (.A(1'b0), .B(ck));
  Switch u_nMS (.A(1'b0), .B(nMS));
  PullUp pullup_3 (.out(pullup_3_out));
  PullUp pullup_4 (.out(pullup_4_out));
  Switch ck_2 (.A(1'b0), .B(pullup_3_out));
  Switch nMS_2 (.A(1'b0), .B(pullup_4_out));
  PullUp pullup_5 (.out(nMR));
  Switch u_nMR (.A(1'b0), .B(nMR));
  PullUp pullup_6 (.out(pullup_6_out));
  Switch nMR_2 (.A(1'b0), .B(pullup_6_out));
  // PolarityAwareLED Q0: pin names not known; wires that end beside it: Q0_p1, 1'b0
  D_FF_AS d_ff_as_1 (.Set(~nMS), .D(d_ff_as_1_nq), .C(ck), .Clr(~nMR), .Q(d_ff_as_1_q), .nQ(d_ff_as_1_nq));
  _7474 _7474_1 (
    .pin1(pullup_6_out), .pin2(_7474_1_pin2), .pin3(pullup_3_out), .pin4(pullup_4_out), .pin5(Q0_p1),
    .pin6(_7474_1_pin2), .pin7(1'b0), .pin8(_7474_1_pin8), .pin9(_7474_1_pin9), .pin10(pullup_4_out),
    .pin11(_7474_1_pin2), .pin12(_7474_1_pin8), .pin13(pullup_6_out), .pin14(1'b1));
  // PolarityAwareLED Q0_2: pin names not known; wires that end beside it: d_ff_as_1_q, 1'b0
  // PolarityAwareLED Q1: pin names not known; wires that end beside it: _7474_1_pin9, 1'b0
  D_FF_AS d_ff_as_2 (.Set(~nMS), .D(d_ff_as_2_nq), .C(d_ff_as_1_nq), .Clr(~nMR), .Q(d_ff_as_2_q), .nQ(d_ff_as_2_nq));
  // PolarityAwareLED Q1_2: pin names not known; wires that end beside it: d_ff_as_2_q, 1'b0
  // PolarityAwareLED Q2: pin names not known; wires that end beside it: Q2_p1, 1'b0
  D_FF_AS d_ff_as_3 (.Set(~nMS), .D(d_ff_as_3_nq), .C(d_ff_as_2_nq), .Clr(~nMR), .Q(d_ff_as_3_q), .nQ(d_ff_as_3_nq));
  _7474 _7474_2 (
    .pin1(pullup_6_out), .pin2(_7474_2_pin2), .pin3(_7474_1_pin8), .pin4(pullup_4_out), .pin5(Q2_p1),
    .pin6(_7474_2_pin2), .pin7(1'b0), .pin8(_7474_2_pin8), .pin9(_7474_2_pin9), .pin10(pullup_4_out),
    .pin11(_7474_2_pin2), .pin12(_7474_2_pin8), .pin13(pullup_6_out), .pin14(1'b1));
  // PolarityAwareLED Q2_2: pin names not known; wires that end beside it: d_ff_as_3_q, 1'b0
  // PolarityAwareLED Q3: pin names not known; wires that end beside it: _7474_2_pin9, 1'b0
  D_FF_AS d_ff_as_4 (.Set(~nMS), .D(d_ff_as_4_nq), .C(d_ff_as_3_nq), .Clr(~nMR), .Q(d_ff_as_4_q), .nQ(d_ff_as_4_nq));
  // PolarityAwareLED Q3_2: pin names not known; wires that end beside it: d_ff_as_4_q, 1'b0

  // Notes on the sheet:
  //   1
  //   2
  //   3
  //   4
  //   5
  //   6
  //   Contador crescente com
  //   incremento em borda de subida!
  //   ***************************************
  //   A importância da pinagem e do
  //   esquema elétrico (diagrama lógico).
  //   ***************************************
  //   10
  //   12
  //   11
  //   13
  //   9
  //   8
endmodule
