// Digital circuit tinkercad-contador-assincrono-detalhes.dig as structural Verilog
module tinkercad_contador_assincrono_detalhes (
);

  wire ck, d_ff_as_1_nq, d_ff_as_2_nq, d_ff_as_3_nq, d_ff_as_4_nq, nMR, nMS, Q0, Q1, Q2, Q3;

  // PolarityAwareLED Q4: pin names not known; wires that end beside it: 1'b1, ck
  PullUp pullup_1 (.out(ck));
  PullUp pullup_2 (.out(nMS));
  Switch u_ck (.A(1'b0), .B(ck));
  Switch u_nMS (.A(1'b0), .B(nMS));
  PullUp pullup_3 (.out(nMR));
  Switch u_nMR (.A(1'b0), .B(nMR));
  D_FF_AS d_ff_as_1 (.Set(~nMS), .D(d_ff_as_1_nq), .C(ck), .Clr(~nMR), .Q(Q0), .nQ(d_ff_as_1_nq));
  // PolarityAwareLED Q0: pin names not known; wires that end beside it: Q0, 1'b0
  D_FF_AS d_ff_as_2 (.Set(~nMS), .D(d_ff_as_2_nq), .C(d_ff_as_1_nq), .Clr(~nMR), .Q(Q1), .nQ(d_ff_as_2_nq));
  // Probe on {Q3, Q2, Q1, Q0}
  // PolarityAwareLED Q1: pin names not known; wires that end beside it: Q1, 1'b0
  D_FF_AS d_ff_as_3 (.Set(~nMS), .D(d_ff_as_3_nq), .C(d_ff_as_2_nq), .Clr(~nMR), .Q(Q2), .nQ(d_ff_as_3_nq));
  // PolarityAwareLED Q2: pin names not known; wires that end beside it: Q2, 1'b0
  Seven_Seg_Hex seven_seg_hex_1 (.d({Q3, Q2, Q1, Q0}), .dp(1'b0));
  D_FF_AS d_ff_as_4 (.Set(~nMS), .D(d_ff_as_4_nq), .C(d_ff_as_3_nq), .Clr(~nMR), .Q(Q3), .nQ(d_ff_as_4_nq));
  // PolarityAwareLED Q3: pin names not known; wires that end beside it: Q3, 1'b0

  // Notes on the sheet:
  //   Questão
  //   Quando ocorre o incremento da contagem?
  //     1) Ao soltar o botão ck, produzindo uma borda de descida.
  //     2) Ao pressionar o botão ck, produzindo uma borda de subida.
  //     3) Ao soltar o botão ck, produzindo uma borda de subida.
  //     4) Ao pressionar o botão ck, produzindo uma borda de descida.
  //     5) Somente ao pressionar e soltar o ~MR antes de se pressionar e soltar o ck.
  //   Contador crescente com
  //   incremento em borda de subida!
  //   Detalhes da montagem no Tinkercad.
endmodule
