// Digital circuit registrador-de-deslocamento.dig as structural Verilog
module registrador_de_deslocamento (
  input  ck,
  input  E,
  input  MS,
  input  MR,
  output Q0,
  output Q1,
  output Q2,
  output Q3
);

  D_FF_AS d_ff_as_1 (.Set(MS), .D(E), .C(ck), .Clr(MR), .Q(Q3));  // open: nQ
  D_FF_AS d_ff_as_2 (.Set(MS), .D(Q3), .C(ck), .Clr(MR), .Q(Q2));  // open: nQ
  D_FF_AS d_ff_as_3 (.Set(MS), .D(Q2), .C(ck), .Clr(MR), .Q(Q1));  // open: nQ
  D_FF_AS d_ff_as_4 (.Set(MS), .D(Q1), .C(ck), .Clr(MR), .Q(Q0));  // open: nQ

  // Notes on the sheet:
  //   E = 1101
endmodule
