// Digital circuit registrador-em-anel.dig as structural Verilog
module registrador_em_anel (
  input  ck,
  input  POR,
  output Q0,
  output Q1,
  output Q2,
  output Q3
);

  D_FF_AS d_ff_as_1 (.Set(POR), .D(Q0), .C(ck), .Clr(1'b0), .Q(Q3));  // open: nQ
  D_FF_AS d_ff_as_2 (.Set(1'b0), .D(Q3), .C(ck), .Clr(POR), .Q(Q2));  // open: nQ
  D_FF_AS d_ff_as_3 (.Set(1'b0), .D(Q2), .C(ck), .Clr(POR), .Q(Q1));  // open: nQ
  D_FF_AS d_ff_as_4 (.Set(1'b0), .D(Q1), .C(ck), .Clr(POR), .Q(Q0));  // open: nQ
endmodule
