// Digital circuit registrador.dig as structural Verilog
module registrador (
  input  ck,
  input  D0,
  input  D1,
  input  D2,
  input  D3,
  input  MS,
  input  MR,
  output Q0,
  output Q1,
  output Q2,
  output Q3
);

  D_FF_AS d_ff_as_1 (.Set(MS), .D(D3), .C(ck), .Clr(MR), .Q(Q3));  // open: nQ
  D_FF_AS d_ff_as_2 (.Set(MS), .D(D2), .C(ck), .Clr(MR), .Q(Q2));  // open: nQ
  D_FF_AS d_ff_as_3 (.Set(MS), .D(D1), .C(ck), .Clr(MR), .Q(Q1));  // open: nQ
  D_FF_AS d_ff_as_4 (.Set(MS), .D(D0), .C(ck), .Clr(MR), .Q(Q0));  // open: nQ

  // Notes on the sheet:
  //   Registrador
endmodule
