// Logisim project Multiplicador de 2 bits.circ as structural Verilog: 5 circuits, main circuit main
module main (
  input  A1,
  input  A0,
  input  B1,
  input  B0,
  output P3,
  output P2,
  output P1,
  output P0
);

  Multiplicador_2_bits___NE_Otimizado multiplicador_2_bits_ne_otimizado_1 (
    .A1(A1), .A0(A0), .B1(B1), .B0(B0), .P3(P3), .P2(P2), .P1(P1), .P0(P0));
endmodule

module Multiplicador_2_bits___Mistas (
  input  A1,
  input  A0,
  input  B1,
  input  B0,
  output P3,
  output P2,
  output P1,
  output P0
);

  wire and_1_out, and_2_out, and_3_out, and_4_out, and_5_out, and_6_out, and_7_out, and_8_out, and_11_out,
       and_12_out, and_13_out, and_14_out, and_15_out, and_16_out, not_1_out, not_2_out, not_3_out,
       not_4_out, not_5_out, not_6_out, or_2_out, or_3_out;

  and and_1 (and_1_out, A1, A0);
  and and_2 (and_2_out, B1, B0);
  and and_3 (and_3_out, A1, not_1_out);
  not not_1 (not_1_out, A0);
  and and_4 (and_4_out, A1, B1);
  not not_2 (not_2_out, B0);
  not not_3 (not_3_out, A1);
  and and_5 (and_5_out, not_3_out, A0);
  and and_6 (and_6_out, A0, B1);
  not not_4 (not_4_out, B0);
  and and_7 (and_7_out, A1, not_5_out);
  not not_5 (not_5_out, A0);
  and and_8 (and_8_out, A1, not_6_out);
  not not_6 (not_6_out, B1);
  and and_9 (P0, A0, B0);
  and and_10 (P3, and_1_out, and_2_out);
  and and_11 (and_11_out, and_3_out, B1);
  and and_12 (and_12_out, and_4_out, not_2_out);
  and and_13 (and_13_out, and_5_out, B1);
  and and_14 (and_14_out, and_6_out, not_4_out);
  and and_15 (and_15_out, and_7_out, B0);
  and and_16 (and_16_out, and_8_out, B0);
  or or_1 (P2, and_11_out, and_12_out);
  or or_2 (or_2_out, and_13_out, and_14_out);
  or or_3 (or_3_out, and_15_out, and_16_out);
  or or_4 (P1, or_2_out, or_3_out);
endmodule

module Multiplicador_2_bits___NE (
  input  A1,
  input  A0,
  input  B1,
  input  B0,
  output P3,
  output P2,
  output P1,
  output P0
);

  wire nand_1_out, nand_2_out, nand_3_out, nand_4_out, nand_5_out, nand_6_out, nand_7_out, nand_8_out,
       nand_9_out, nand_10_out, nand_11_out, nand_12_out, nand_13_out, nand_14_out, nand_15_out, nand_17_out,
       nand_18_out, nand_19_out, nand_20_out, nand_21_out, nand_22_out, nand_23_out, nand_24_out,
       nand_25_out, nand_27_out, nand_28_out, nand_29_out, nand_30_out, nand_31_out, nand_32_out,
       nand_34_out, nand_35_out, nand_36_out, nand_37_out;

  nand nand_1 (nand_1_out, A1, A0);
  nand nand_2 (nand_2_out, B1, B0);
  nand nand_3 (nand_3_out, A0, A0);
  nand nand_4 (nand_4_out, A1, A1);
  nand nand_5 (nand_5_out, A0, A0);
  nand nand_6 (nand_6_out, B1, B1);
  nand nand_7 (nand_7_out, A0, B0);
  nand nand_8 (nand_8_out, nand_1_out, nand_1_out);
  nand nand_9 (nand_9_out, nand_2_out, nand_2_out);
  nand nand_10 (nand_10_out, A1, nand_3_out);
  nand nand_11 (nand_11_out, A1, B1);
  nand nand_12 (nand_12_out, nand_4_out, A0);
  nand nand_13 (nand_13_out, A0, B1);
  nand nand_14 (nand_14_out, A1, nand_5_out);
  nand nand_15 (nand_15_out, A1, nand_6_out);
  nand nand_16 (P0, nand_7_out, nand_7_out);
  nand nand_17 (nand_17_out, nand_8_out, nand_9_out);
  nand nand_18 (nand_18_out, nand_10_out, nand_10_out);
  nand nand_19 (nand_19_out, nand_11_out, nand_11_out);
  nand nand_20 (nand_20_out, B0, B0);
  nand nand_21 (nand_21_out, nand_12_out, nand_12_out);
  nand nand_22 (nand_22_out, nand_13_out, nand_13_out);
  nand nand_23 (nand_23_out, B0, B0);
  nand nand_24 (nand_24_out, nand_14_out, nand_14_out);
  nand nand_25 (nand_25_out, nand_15_out, nand_15_out);
  nand nand_26 (P3, nand_17_out, nand_17_out);
  nand nand_27 (nand_27_out, nand_18_out, B1);
  nand nand_28 (nand_28_out, nand_19_out, nand_20_out);
  nand nand_29 (nand_29_out, nand_21_out, B1);
  nand nand_30 (nand_30_out, nand_22_out, nand_23_out);
  nand nand_31 (nand_31_out, nand_24_out, B0);
  nand nand_32 (nand_32_out, nand_25_out, B0);
  nand nand_33 (P2, nand_27_out, nand_28_out);
  nand nand_34 (nand_34_out, nand_29_out, nand_30_out);
  nand nand_35 (nand_35_out, nand_31_out, nand_32_out);
  nand nand_36 (nand_36_out, nand_34_out, nand_34_out);
  nand nand_37 (nand_37_out, nand_35_out, nand_35_out);
  nand nand_38 (P1, nand_36_out, nand_37_out);
endmodule

module Multiplicador_2_bits___NE_Otimizado (
  input  A1,
  input  A0,
  input  B1,
  input  B0,
  output P3,
  output P2,
  output P1,
  output P0
);

  wire nand_1_out, nand_2_out, nand_3_out, nand_4_out, nand_5_out, nand_7_out, nand_8_out, nand_9_out,
       nand_10_out, nand_11_out, nand_12_out;

  nand nand_1 (nand_1_out, A1, B1);
  nand nand_2 (nand_2_out, A0, B0);
  nand nand_3 (nand_3_out, A0, B1);
  nand nand_4 (nand_4_out, A1, B0);
  nand nand_5 (nand_5_out, nand_1_out, nand_1_out);
  nand nand_6 (P0, nand_2_out, nand_2_out);
  nand nand_7 (nand_7_out, nand_3_out, nand_3_out);
  nand nand_8 (nand_8_out, nand_4_out, nand_4_out);
  nand nand_9 (nand_9_out, nand_5_out, P0);
  nand nand_10 (nand_10_out, nand_5_out, nand_2_out);
  nand nand_11 (nand_11_out, nand_7_out, nand_4_out);
  nand nand_12 (nand_12_out, nand_3_out, nand_8_out);
  nand nand_13 (P3, nand_9_out, nand_9_out);
  nand nand_14 (P2, nand_10_out, nand_10_out);
  nand nand_15 (P1, nand_11_out, nand_12_out);
endmodule

module Multiplicador_2_bits___com_Meio_Somandor (
  input  A1,
  input  A0,
  input  B1,
  input  B0,
  output P3,
  output P2,
  output P1,
  output P0
);

  wire and_2_out, and_3_out, and_4_out, and_5_out;

  and and_1 (P0, A0, B0);
  and and_2 (and_2_out, A1, B0);
  and and_3 (and_3_out, A0, B1);
  and and_4 (and_4_out, A1, B1);
  and and_5 (and_5_out, and_2_out, and_3_out);
  xor xor_1 (P1, and_2_out, and_3_out);
  and and_6 (P3, and_5_out, and_4_out);
  xor xor_2 (P2, and_5_out, and_4_out);
endmodule
