// Logisim project multiplicador-4-bits.circ as structural Verilog: 7 circuits, main circuit Circuito Multiplicador
module Circuito_Multiplicador (
  input  MSB,
  input  in_2,
  input  in_3,
  input  LSB,
  input  LDa,
  input  LDb,
  input  Clock__CKa,
  input  Clock__CKb,
  input  Clock__cks,
  input  CLRs,
  input  LDL,
  output RBZ,
  output RB0,
  output out_14,
  output out_15,
  output out_16,
  output out_17,
  output out_18,
  output out_19,
  output out_20,
  output out_21
);

  wire decod_hexadecimal_1_s1, decod_hexadecimal_1_s2, decod_hexadecimal_1_s3, decod_hexadecimal_1_s4,
       decod_hexadecimal_1_s5, decod_hexadecimal_1_s6, decod_hexadecimal_1_s7, decod_hexadecimal_2_s1,
       decod_hexadecimal_2_s2, decod_hexadecimal_2_s3, decod_hexadecimal_2_s4, decod_hexadecimal_2_s5,
       decod_hexadecimal_2_s6, decod_hexadecimal_2_s7, not_1_out, not_2_out, RA_q0, RA_q1, RA_q2, RA_q3,
       RA_q4, RA_q5, RA_q6, RA_q7, RB_q0, RB_q1, RB_q2, RSoma_q0, RSoma_q1, RSoma_q2, RSoma_q3, RSoma_q4,
       RSoma_q5, RSoma_q6, RSoma_q7, \somatória_1_out_17 , \somatória_1_out_18 , \somatória_1_out_19 ,
       \somatória_1_out_20 , \somatória_1_out_21 , \somatória_1_out_22 , \somatória_1_out_23 ,
       \somatória_1_out_24 ;

  not not_1 (not_1_out, LDa);
  Shift_Register RA (
    .shift(not_1_out), .in(1'b0), .clk(Clock__CKa), .load(LDa), .d0(LSB), .q0(RA_q0), .d1(in_3), .q1(RA_q1),
    .d2(in_2), .q2(RA_q2), .d3(MSB), .q3(RA_q3), .d4(1'b0), .q4(RA_q4), .d5(1'b0), .q5(RA_q5), .d6(1'b0),
    .q6(RA_q6), .d7(1'b0), .q7(RA_q7));  // open: out, clr
  \Somatória  \somatória_1  (
    .in_1(RSoma_q0), .in_9(RA_q7), .in_2(RSoma_q1), .in_10(RA_q6), .in_3(RSoma_q2), .in_11(RA_q5),
    .in_4(RSoma_q3), .in_12(RA_q4), .in_5(RSoma_q4), .in_13(RA_q3), .in_6(RSoma_q5), .in_14(RA_q2),
    .in_7(RSoma_q6), .in_15(RA_q1), .in_8(RSoma_q7), .in_16(RA_q0), .out_17(\somatória_1_out_17 ),
    .out_18(\somatória_1_out_18 ), .out_19(\somatória_1_out_19 ), .out_20(\somatória_1_out_20 ),
    .out_21(\somatória_1_out_21 ), .out_22(\somatória_1_out_22 ), .out_23(\somatória_1_out_23 ),
    .out_24(\somatória_1_out_24 ));
  Shift_Register RSoma (
    .clk(Clock__cks), .load(1'b1), .clr(CLRs), .d0(\somatória_1_out_17 ), .q0(RSoma_q0),
    .d1(\somatória_1_out_18 ), .q1(RSoma_q1), .d2(\somatória_1_out_19 ), .q2(RSoma_q2),
    .d3(\somatória_1_out_20 ), .q3(RSoma_q3), .d4(\somatória_1_out_21 ), .q4(RSoma_q4),
    .d5(\somatória_1_out_22 ), .q5(RSoma_q5), .d6(\somatória_1_out_23 ), .q6(RSoma_q6),
    .d7(\somatória_1_out_24 ), .q7(RSoma_q7));  // open: shift, in, out
  Shift_Register shift_register_1 (
    .clk(LDL), .load(1'b1), .d0(RSoma_q0), .q0(out_21), .d1(RSoma_q1), .q1(out_19), .d2(RSoma_q2),
    .q2(out_17), .d3(RSoma_q3), .q3(out_15), .d4(RSoma_q4), .q4(out_20), .d5(RSoma_q5), .q5(out_18),
    .d6(RSoma_q6), .q6(out_16), .d7(RSoma_q7), .q7(out_14));  // open: shift, in, out, clr
  _7_Segment_Display u_7_segment_display_1 (
    .g(decod_hexadecimal_1_s1), .f(decod_hexadecimal_1_s2), .a(decod_hexadecimal_1_s3),
    .b(decod_hexadecimal_1_s4), .e(decod_hexadecimal_1_s7), .d(decod_hexadecimal_1_s6),
    .c(decod_hexadecimal_1_s5));  // open: dp
  Decod__Hexadecimal decod_hexadecimal_1 (
    .b0(out_21), .b1(out_19), .b2(out_17), .b3(out_15), .s1(decod_hexadecimal_1_s1),
    .s2(decod_hexadecimal_1_s2), .s3(decod_hexadecimal_1_s3), .s4(decod_hexadecimal_1_s4),
    .s5(decod_hexadecimal_1_s5), .s6(decod_hexadecimal_1_s6), .s7(decod_hexadecimal_1_s7));
  Decod__Hexadecimal decod_hexadecimal_2 (
    .b0(out_20), .b1(out_18), .b2(out_16), .b3(out_14), .s1(decod_hexadecimal_2_s1),
    .s2(decod_hexadecimal_2_s2), .s3(decod_hexadecimal_2_s3), .s4(decod_hexadecimal_2_s4),
    .s5(decod_hexadecimal_2_s5), .s6(decod_hexadecimal_2_s6), .s7(decod_hexadecimal_2_s7));
  _7_Segment_Display u_7_segment_display_2 (
    .g(decod_hexadecimal_2_s1), .f(decod_hexadecimal_2_s2), .a(decod_hexadecimal_2_s3),
    .b(decod_hexadecimal_2_s4), .e(decod_hexadecimal_2_s7), .d(decod_hexadecimal_2_s6),
    .c(decod_hexadecimal_2_s5));  // open: dp
  not not_2 (not_2_out, LDb);
  Shift_Register #(.length(4)) RB (
    .shift(not_2_out), .in(1'b0), .clk(Clock__CKb), .load(LDb), .d0(MSB), .q0(RB_q0), .d1(in_2), .q1(RB_q1),
    .d2(in_3), .q2(RB_q2), .d3(LSB), .q3(RB0));  // open: out, clr
  nor nor_1 (RBZ, RB0, RB_q2, RB_q1, RB_q0);

  // Notes on the sheet:
  //   Carga
endmodule

module \Somatória  (
  input  in_1,
  input  in_2,
  input  in_3,
  input  in_4,
  input  in_5,
  input  in_6,
  input  in_7,
  input  in_8,
  input  in_9,
  input  in_10,
  input  in_11,
  input  in_12,
  input  in_13,
  input  in_14,
  input  in_15,
  input  in_16,
  output out_17,
  output out_18,
  output out_19,
  output out_20,
  output out_21,
  output out_22,
  output out_23,
  output out_24
);

  wire adder_2_cout, adder_3_cout, adder_4_cout, adder_5_cout, adder_6_cout, adder_7_cout, adder_8_cout;

  Adder #(.width(1)) adder_1 (.a(in_9), .b(in_1), .out(out_17), .cin(adder_2_cout));  // open: cout
  Adder #(.width(1)) adder_2 (.a(in_10), .b(in_2), .out(out_18), .cin(adder_3_cout), .cout(adder_2_cout));
  Adder #(.width(1)) adder_3 (.a(in_11), .b(in_3), .out(out_19), .cin(adder_4_cout), .cout(adder_3_cout));
  Adder #(.width(1)) adder_4 (.a(in_12), .b(in_4), .out(out_20), .cin(adder_5_cout), .cout(adder_4_cout));
  Adder #(.width(1)) adder_5 (.a(in_13), .b(in_5), .out(out_21), .cin(adder_6_cout), .cout(adder_5_cout));
  Adder #(.width(1)) adder_6 (.a(in_14), .b(in_6), .out(out_22), .cin(adder_7_cout), .cout(adder_6_cout));
  Adder #(.width(1)) adder_7 (.a(in_15), .b(in_7), .out(out_23), .cin(adder_8_cout), .cout(adder_7_cout));
  Adder #(.width(1)) adder_8 (.a(in_16), .b(in_8), .out(out_24), .cout(adder_8_cout));  // open: cin
endmodule

module Decod__Hexadecimal (
  input  b0,
  input  b1,
  input  b2,
  input  b3,
  output s1,
  output s2,
  output s3,
  output s4,
  output s5,
  output s6,
  output s7
);

  wire and_1_out, and_2_out, and_3_out, and_4_out, and_5_out, and_6_out, and_7_out, and_8_out, and_9_out,
       and_10_out, and_11_out, and_12_out, and_13_out, and_14_out, and_15_out, and_16_out, and_17_out,
       and_18_out, and_19_out, and_20_out, and_21_out, and_22_out, and_23_out, and_24_out, and_25_out,
       and_26_out, and_27_out, and_28_out, and_29_out, and_30_out, and_31_out, and_32_out, and_33_out,
       and_34_out, and_35_out, not_1_out, not_2_out, not_3_out, not_4_out, not_5_out, not_6_out, not_7_out,
       not_8_out, not_9_out, not_10_out, not_11_out, not_12_out, not_13_out, not_14_out, not_15_out,
       not_16_out, not_17_out, not_18_out, not_19_out, not_20_out, not_21_out, not_22_out, not_23_out,
       not_24_out, not_25_out, not_26_out, not_27_out, not_28_out, not_29_out, not_30_out, not_31_out,
       not_32_out, not_33_out, not_34_out, not_35_out, not_36_out, not_37_out, not_38_out, not_39_out,
       not_40_out, not_41_out, not_42_out, not_43_out;

  not not_1 (not_1_out, b1);
  and and_1 (and_1_out, not_1_out, b2);
  and and_2 (and_2_out, b2, not_2_out);
  not not_2 (not_2_out, b3);
  not not_3 (not_3_out, b0);
  and and_3 (and_3_out, not_3_out, b1, not_4_out);
  not not_4 (not_4_out, b2);
  and and_4 (and_4_out, b0, not_5_out);
  not not_5 (not_5_out, b1);
  and and_5 (and_5_out, b0, b3);
  not not_6 (not_6_out, b2);
  and and_6 (and_6_out, not_6_out, not_7_out);
  not not_7 (not_7_out, b3);
  not not_8 (not_8_out, b0);
  and and_7 (and_7_out, not_8_out, b1, not_9_out);
  not not_9 (not_9_out, b2);
  and and_8 (and_8_out, b1, not_10_out);
  not not_10 (not_10_out, b3);
  and and_9 (and_9_out, b0, not_11_out);
  not not_11 (not_11_out, b1);
  and and_10 (and_10_out, b0, b2);
  not not_12 (not_12_out, b1);
  and and_11 (and_11_out, not_12_out, not_13_out);
  not not_13 (not_13_out, b3);
  not not_14 (not_14_out, b0);
  and and_12 (and_12_out, not_14_out, b2);
  not not_15 (not_15_out, b0);
  and and_13 (and_13_out, not_15_out, b1, b3);
  and and_14 (and_14_out, b1, b2);
  not not_16 (not_16_out, b1);
  and and_15 (and_15_out, b0, not_16_out, not_17_out);
  not not_17 (not_17_out, b2);
  and and_16 (and_16_out, b0, not_18_out);
  not not_18 (not_18_out, b3);
  not not_19 (not_19_out, b0);
  and and_17 (and_17_out, not_19_out, not_20_out);
  not not_20 (not_20_out, b1);
  not not_21 (not_21_out, b0);
  and and_18 (and_18_out, not_21_out, not_22_out, not_23_out);
  not not_22 (not_22_out, b2);
  not not_23 (not_23_out, b3);
  not not_24 (not_24_out, b1);
  and and_19 (and_19_out, not_24_out, not_25_out);
  not not_25 (not_25_out, b3);
  not not_26 (not_26_out, b0);
  and and_20 (and_20_out, not_26_out, b2, b3);
  not not_27 (not_27_out, b2);
  and and_21 (and_21_out, b0, not_27_out, b3);
  not not_28 (not_28_out, b0);
  and and_22 (and_22_out, not_28_out, not_29_out);
  not not_29 (not_29_out, b2);
  not not_30 (not_30_out, b0);
  and and_23 (and_23_out, not_30_out, b3);
  not not_31 (not_31_out, b2);
  and and_24 (and_24_out, not_31_out, b3);
  not not_32 (not_32_out, b0);
  and and_25 (and_25_out, not_32_out, b1);
  and and_26 (and_26_out, b0, not_33_out);
  not not_33 (not_33_out, b1);
  not not_34 (not_34_out, b0);
  not not_35 (not_35_out, b1);
  and and_27 (and_27_out, not_34_out, not_35_out, not_36_out);
  not not_36 (not_36_out, b3);
  not not_37 (not_37_out, b1);
  and and_28 (and_28_out, not_37_out, b2, b3);
  not not_38 (not_38_out, b2);
  and and_29 (and_29_out, b1, not_38_out, b3);
  and and_30 (and_30_out, b1, b2, not_39_out);
  not not_39 (not_39_out, b3);
  and and_31 (and_31_out, b0, not_40_out);
  not not_40 (not_40_out, b2);
  not not_41 (not_41_out, b1);
  and and_32 (and_32_out, not_41_out, not_42_out);
  not not_42 (not_42_out, b3);
  and and_33 (and_33_out, b2, not_43_out);
  not not_43 (not_43_out, b3);
  and and_34 (and_34_out, b0, b2);
  and and_35 (and_35_out, b0, b1);
  or or_1 (s1, and_1_out, and_2_out, and_3_out, and_4_out, and_5_out);
  or or_2 (s2, and_6_out, and_7_out, and_8_out, and_9_out, and_10_out);
  or or_3 (s4, and_17_out, and_18_out, and_19_out, and_20_out, and_21_out);
  or or_4 (s5, and_22_out, and_23_out, and_24_out, and_25_out, and_26_out);
  or or_5 (s6, and_27_out, and_28_out, and_29_out, and_30_out, and_31_out);
  or or_6 (s7, and_32_out, and_33_out, and_34_out, and_35_out);
  or or_7 (s3, and_11_out, and_12_out, and_13_out, and_14_out, and_15_out, and_16_out);
endmodule

module Flip_Flops (
  input  DV,
  input  RB0,
  input  RBZ,
  input  ck,
  input  POR,
  output Q2,
  output Q1,
  output Q0
);

  wire and_1_out, and_2_out, and_3_out, and_4_out, not_1_out, not_2_out, not_3_out, not_4_out, not_5_out,
       or_1_out, or_2_out, or_3_out, or_4_out;

  not not_1 (not_1_out, DV);
  not not_2 (not_2_out, Q0);
  not not_3 (not_3_out, RBZ);
  not not_4 (not_4_out, Q1);
  not not_5 (not_5_out, DV);
  and and_1 (and_1_out, not_1_out, Q0);
  and and_2 (and_2_out, RBZ, not_2_out);
  and and_3 (and_3_out, not_3_out, Q1);
  and and_4 (and_4_out, DV, not_4_out);
  or or_1 (or_1_out, not_5_out, Q1);
  or or_2 (or_2_out, and_1_out, Q1);
  or or_3 (or_3_out, Q2, and_2_out);
  or or_4 (or_4_out, and_3_out, and_4_out);
  J_K_Flip_Flop j_k_ff_1 (.J(1'b0), .clk(ck), .K(1'b1), .Q(Q2), .preset(POR), .en(1'b1), .reset(1'b0));  // open: Qn
  J_K_Flip_Flop j_k_ff_2 (
    .J(or_2_out), .clk(ck), .K(or_3_out), .Q(Q1), .preset(POR), .en(1'b1), .reset(1'b0));  // open: Qn
  J_K_Flip_Flop j_k_ff_3 (
    .J(or_4_out), .clk(ck), .K(or_1_out), .Q(Q0), .preset(POR), .en(1'b1), .reset(1'b0));  // open: Qn
endmodule

module Saida (
  input  DV,
  input  RB0,
  input  RBZ,
  input  Q2,
  input  Q1,
  input  Q0,
  output CKa,
  output LDa,
  output CKb,
  output LDb,
  output CKs,
  output CLRs,
  output LDL
);

  wire and_1_out, and_2_out, and_4_out, and_5_out, and_8_out, and_9_out, and_10_out, and_11_out, not_1_out,
       not_2_out, not_3_out, not_4_out, not_5_out, not_6_out, not_7_out, not_8_out, not_9_out, not_10_out,
       not_11_out, not_12_out, not_13_out, not_14_out, not_15_out, not_16_out, not_17_out, not_18_out,
       not_19_out, not_20_out, not_21_out, not_22_out, not_23_out;

  not not_1 (not_1_out, Q2);
  not not_2 (not_2_out, Q2);
  not not_3 (not_3_out, Q1);
  not not_4 (not_4_out, Q0);
  not not_5 (not_5_out, Q2);
  not not_6 (not_6_out, Q1);
  not not_7 (not_7_out, Q0);
  not not_8 (not_8_out, DV);
  not not_9 (not_9_out, Q2);
  not not_10 (not_10_out, Q2);
  not not_11 (not_11_out, Q2);
  not not_12 (not_12_out, Q1);
  not not_13 (not_13_out, RBZ);
  not not_14 (not_14_out, Q2);
  not not_15 (not_15_out, Q0);
  not not_16 (not_16_out, Q2);
  not not_17 (not_17_out, Q1);
  not not_18 (not_18_out, DV);
  not not_19 (not_19_out, Q2);
  not not_20 (not_20_out, Q1);
  not not_21 (not_21_out, Q0);
  not not_22 (not_22_out, Q2);
  not not_23 (not_23_out, Q0);
  and and_1 (and_1_out, not_1_out, Q1, Q0);
  and and_2 (and_2_out, DV, not_2_out, not_3_out, not_4_out);
  and and_3 (LDa, not_5_out, not_6_out, not_7_out);
  and and_4 (and_4_out, not_8_out, not_9_out, Q0);
  and and_5 (and_5_out, not_10_out, Q1, Q0);
  and and_6 (LDb, not_11_out, not_12_out, Q0);
  and and_7 (CKs, RB0, not_13_out, not_14_out, Q1, not_15_out);
  and and_8 (and_8_out, Q2, Q1, Q0);
  and and_9 (and_9_out, DV, not_16_out, not_17_out, Q0);
  and and_10 (and_10_out, not_18_out, not_19_out, not_20_out, not_21_out);
  and and_11 (and_11_out, RBZ, not_22_out, Q1, not_23_out);
  or or_1 (CKa, and_1_out, and_2_out);
  or or_2 (CKb, and_4_out, and_5_out);
  or or_3 (CLRs, and_8_out, and_9_out);
  or or_4 (LDL, and_10_out, and_11_out);
endmodule

module Maquina_de_Estados (
  input  DV,
  input  RB0,
  input  RBZ,
  input  ck,
  input  POR,
  output out_6,
  output out_7,
  output out_8,
  output out_9,
  output out_10,
  output out_11,
  output out_12
);

  wire ffs_1_q0, ffs_1_q1, ffs_1_q2;

  Flip_Flops ffs_1 (.DV(DV), .RB0(RB0), .RBZ(RBZ), .ck(ck), .POR(POR), .Q2(ffs_1_q2), .Q1(ffs_1_q1), .Q0(ffs_1_q0));
  Saida saida_1 (
    .DV(DV), .RB0(RB0), .RBZ(RBZ), .Q2(ffs_1_q2), .Q1(ffs_1_q1), .Q0(ffs_1_q0), .CKa(out_6), .LDa(out_7),
    .CKb(out_8), .LDb(out_9), .CKs(out_10), .CLRs(out_11), .LDL(out_12));
endmodule

module Circuito_Final (
  input  in_1,
  input  Dado,
  input  in_3,
  input  in_4
);

  wire \Botão_out , circuito_multiplicador_1_out_14, circuito_multiplicador_1_out_15,
       circuito_multiplicador_1_out_16, circuito_multiplicador_1_out_17, circuito_multiplicador_1_out_18,
       circuito_multiplicador_1_out_19, circuito_multiplicador_1_out_20, circuito_multiplicador_1_out_21,
       circuito_multiplicador_1_rb0, circuito_multiplicador_1_rbz, CKme_out, DA, DB, decod_hexadecimal_1_s1,
       decod_hexadecimal_1_s2, decod_hexadecimal_1_s3, decod_hexadecimal_1_s4, decod_hexadecimal_1_s5,
       decod_hexadecimal_1_s6, decod_hexadecimal_1_s7, decod_hexadecimal_2_s1, decod_hexadecimal_2_s2,
       decod_hexadecimal_2_s3, decod_hexadecimal_2_s4, decod_hexadecimal_2_s5, decod_hexadecimal_2_s6,
       decod_hexadecimal_2_s7, maquina_de_estados_1_out_6, maquina_de_estados_1_out_7,
       maquina_de_estados_1_out_8, maquina_de_estados_1_out_9, maquina_de_estados_1_out_10,
       maquina_de_estados_1_out_11, maquina_de_estados_1_out_12, POR;

  LED A (.in(DA));
  LED B (.in(DB));
  Button \Botão  (.out(\Botão_out ));
  Button u_POR (.out(POR));
  T_Flip_Flop #(.trigger("falling")) t_ff_1 (
    .clk(\Botão_out ), .T(1'b1), .Q(DB), .Qn(DA), .preset(1'b0), .reset(POR));  // open: en
  Clock CKme (.out(CKme_out));
  Maquina_de_Estados maquina_de_estados_1 (
    .DV(DB), .RB0(circuito_multiplicador_1_rb0), .RBZ(circuito_multiplicador_1_rbz),
    .out_6(maquina_de_estados_1_out_6), .out_7(maquina_de_estados_1_out_7),
    .out_8(maquina_de_estados_1_out_8), .out_9(maquina_de_estados_1_out_9),
    .out_10(maquina_de_estados_1_out_10), .out_11(maquina_de_estados_1_out_11),
    .out_12(maquina_de_estados_1_out_12), .ck(CKme_out), .POR(POR));
  Circuito_Multiplicador circuito_multiplicador_1 (
    .LDa(maquina_de_estados_1_out_7), .LDb(maquina_de_estados_1_out_9),
    .Clock__CKa(maquina_de_estados_1_out_6), .Clock__CKb(maquina_de_estados_1_out_8),
    .Clock__cks(maquina_de_estados_1_out_10), .CLRs(maquina_de_estados_1_out_11),
    .LDL(maquina_de_estados_1_out_12), .RBZ(circuito_multiplicador_1_rbz), .MSB(in_1), .in_2(Dado),
    .in_3(in_3), .LSB(in_4), .RB0(circuito_multiplicador_1_rb0), .out_14(circuito_multiplicador_1_out_14),
    .out_16(circuito_multiplicador_1_out_16), .out_18(circuito_multiplicador_1_out_18),
    .out_20(circuito_multiplicador_1_out_20), .out_15(circuito_multiplicador_1_out_15),
    .out_17(circuito_multiplicador_1_out_17), .out_19(circuito_multiplicador_1_out_19),
    .out_21(circuito_multiplicador_1_out_21));
  Decod__Hexadecimal decod_hexadecimal_1 (
    .b0(circuito_multiplicador_1_out_21), .b1(circuito_multiplicador_1_out_19),
    .b2(circuito_multiplicador_1_out_17), .b3(circuito_multiplicador_1_out_15), .s1(decod_hexadecimal_1_s1),
    .s2(decod_hexadecimal_1_s2), .s3(decod_hexadecimal_1_s3), .s4(decod_hexadecimal_1_s4),
    .s5(decod_hexadecimal_1_s5), .s6(decod_hexadecimal_1_s6), .s7(decod_hexadecimal_1_s7));
  _7_Segment_Display u_7_segment_display_1 (
    .g(decod_hexadecimal_1_s1), .f(decod_hexadecimal_1_s2), .a(decod_hexadecimal_1_s3),
    .b(decod_hexadecimal_1_s4), .e(decod_hexadecimal_1_s7), .d(decod_hexadecimal_1_s6),
    .c(decod_hexadecimal_1_s5));  // open: dp
  Decod__Hexadecimal decod_hexadecimal_2 (
    .b0(circuito_multiplicador_1_out_20), .b1(circuito_multiplicador_1_out_18),
    .b2(circuito_multiplicador_1_out_16), .b3(circuito_multiplicador_1_out_14), .s1(decod_hexadecimal_2_s1),
    .s2(decod_hexadecimal_2_s2), .s3(decod_hexadecimal_2_s3), .s4(decod_hexadecimal_2_s4),
    .s5(decod_hexadecimal_2_s5), .s6(decod_hexadecimal_2_s6), .s7(decod_hexadecimal_2_s7));
  _7_Segment_Display u_7_segment_display_2 (
    .g(decod_hexadecimal_2_s1), .f(decod_hexadecimal_2_s2), .a(decod_hexadecimal_2_s3),
    .b(decod_hexadecimal_2_s4), .e(decod_hexadecimal_2_s7), .d(decod_hexadecimal_2_s6),
    .c(decod_hexadecimal_2_s5));  // open: dp

  // Other names for the same wires on the sheet: D0 = in_4; D1 = in_3; D2 = Dado; D3 = in_1

  // Notes on the sheet:
  //   Digitar o dado:
  //   1 - Aperte "POR"
  //   3 - Aperte o "Botão"
  //   5 - Aperte o "Botão"
  //   2 - Digite um dos números a ser multiplicado
  //   4 - Digite o outro número a ser multiplicado
  //   (Resultado em Hexadecimal)
endmodule
