// Digital circuit misturador-de-agua-fria-e-quente#vaf1-com-defeito.dig as structural Verilog
module misturador_de_agua_fria_e_quente_vaf1_com_defeito (
  input  SAF,
  input  SAQ,
  input  TAF,
  input  TAQ,
  output VAF1
);

  wire and_1_out, and_2_out, not_1_out, not_2_out, not_3_out, not_4_out;

  not not_1 (not_1_out, SAF);
  not not_2 (not_2_out, SAQ);
  not not_3 (not_3_out, TAF);
  not not_4 (not_4_out, TAQ);
  and and_1 (and_1_out, not_2_out, TAF);
  and and_2 (and_2_out, TAF, TAQ);
  or or_1 (VAF1, and_1_out, and_2_out);
endmodule
