// Digital circuit misturador-de-agua-fria-e-quente#vaf1-portas-ne.dig as structural Verilog
module misturador_de_agua_fria_e_quente_vaf1_portas_ne (
  input  SAF,
  input  SAQ,
  input  TAF,
  input  TAQ,
  output VAF1
);

  wire nand_1_out, nand_2_out, not_1_out, not_2_out, not_3_out, not_4_out;

  not not_1 (not_1_out, SAF);
  not not_2 (not_2_out, SAQ);
  not not_3 (not_3_out, TAF);
  not not_4 (not_4_out, TAQ);
  nand nand_1 (nand_1_out, not_2_out, not_3_out);
  nand nand_2 (nand_2_out, not_3_out, TAQ);
  nand nand_3 (VAF1, nand_1_out, nand_2_out);

  // Notes on the sheet:
  //   SAF: default 1
  //   SAQ: default 1
endmodule
