// Digital circuit contador-assincrono-incompleto.dig as structural Verilog
module contador_assincrono_incompleto (
  input  ck,
  output fs
);

  wire Q0_q, Q1_q, Q2_q;

  JK_FF_AS Q0 (.J(1'b1), .C(~ck), .K(1'b1), .Q(Q0_q));  // open: Set, Clr, nQ
  JK_FF_AS Q1 (.J(1'b1), .C(~Q0_q), .K(1'b1), .Q(Q1_q));  // open: Set, Clr, nQ
  JK_FF_AS Q2 (.J(1'b1), .C(~Q1_q), .K(1'b1), .Q(Q2_q));  // open: Set, Clr, nQ
  JK_FF_AS Q3 (.J(1'b1), .C(~Q2_q), .K(1'b1), .Q(fs));  // open: Set, Clr, nQ
endmodule
