// Digital circuit contador-sincrono.dig as structural Verilog
module contador_sincrono (
  input  ck,
  input  POR,
  output Q0,
  output Q1,
  output Q2
);

  wire jk_ff_as_1_nq, nQ1, or_1_out;

  or or_1 (or_1_out, nQ1, Q0);
  JK_FF_AS jk_ff_as_1 (.Set(1'b0), .J(or_1_out), .C(ck), .K(1'b1), .Clr(POR), .Q(Q2), .nQ(jk_ff_as_1_nq));
  JK_FF_AS jk_ff_as_2 (.Set(POR), .J(1'b1), .C(ck), .K(jk_ff_as_1_nq), .Clr(1'b0), .Q(Q1), .nQ(nQ1));
  JK_FF_AS jk_ff_as_3 (.Set(POR), .J(nQ1), .C(ck), .K(nQ1), .Clr(1'b0), .Q(Q0));  // open: nQ
endmodule
