// Digital circuit registrador-de-deslocamento.dig as structural Verilog
module registrador_de_deslocamento (
  input  ck,
  input  MS,
  output Q0,
  output Q1,
  output Q2,
  output Q3
);

  D_FF_AS d_ff_as_1 (.Set(1'b0), .D(Q0), .C(ck), .Clr(MS), .Q(Q3));  // open: nQ
  D_FF_AS #(.Default(1)) d_ff_as_2 (.Set(MS), .D(Q3), .C(ck), .Clr(1'b0), .Q(Q2));  // open: nQ
  D_FF_AS #(.Default(1)) d_ff_as_3 (.Set(MS), .D(Q2), .C(ck), .Clr(1'b0), .Q(Q1));  // open: nQ
  D_FF_AS #(.Default(1)) d_ff_as_4 (.Set(MS), .D(Q1), .C(ck), .Clr(1'b0), .Q(Q0));  // open: nQ

  // Notes on the sheet:
  //   MS: default 1
endmodule

/* Test case:
MS ck Q3 Q2 Q1 Q0
1 1 0 1 1 1
1 1 0 1 1 1
0 0 0 1 1 1
0 1 1 0 1 1
0 0 1 0 1 1
0 1 1 1 0 1
0 0 1 1 0 1
0 1 1 1 1 0
0 0 1 1 1 0
0 1 0 1 1 1
0 0 0 1 1 1
0 1 1 0 1 1
0 0 1 0 1 1
0 1 1 1 0 1
0 0 1 1 0 1
0 1 1 1 1 0
*/
