// Digital circuit contador-assincrono-completo.dig as structural Verilog
module contador_assincrono_completo (
  input  ck,
  input  POR,
  output fs,
  output Q0,
  output Q1,
  output Q2,
  output Q3
);

  wire and_1_out, or_1_out;

  JK_FF_AS #(.Default(1)) u_Q0 (.Set(or_1_out), .J(1'b1), .C(~ck), .K(1'b1), .Clr(1'b0), .Q(Q0));  // open: nQ
  or or_1 (or_1_out, POR, and_1_out);
  JK_FF_AS #(.Default(1)) u_Q1 (.Set(or_1_out), .J(1'b1), .C(~Q0), .K(1'b1), .Clr(1'b0), .Q(Q1));  // open: nQ
  and and_1 (and_1_out, fs, Q2, Q1, Q0);
  JK_FF_AS u_Q2 (.Set(1'b0), .J(1'b1), .C(~Q1), .K(1'b1), .Clr(or_1_out), .Q(Q2));  // open: nQ
  JK_FF_AS u_Q3 (.Set(1'b0), .J(1'b1), .C(~Q2), .K(1'b1), .Clr(or_1_out), .Q(fs));  // open: nQ

  assign Q3 = fs;

  // Notes on the sheet:
  //   POR: default 1
endmodule
