// Digital circuit contador-sincrono.dig as structural Verilog
module contador_sincrono (
  input  ck,
  input  POR,
  output Q0,
  output Q1,
  output Q2
);

  wire and_1_out, nQ0, nQ1, nQ2;

  JK_FF_AS jk_ff_as_1 (.Set(POR), .J(nQ0), .C(ck), .K(nQ1), .Clr(1'b0), .Q(Q2), .nQ(nQ2));
  JK_FF_AS jk_ff_as_2 (.Set(1'b0), .J(1'b1), .C(ck), .K(Q0), .Clr(POR), .Q(Q1), .nQ(nQ1));
  and and_1 (and_1_out, nQ2, nQ1);
  JK_FF_AS jk_ff_as_3 (.Set(POR), .J(1'b1), .C(ck), .K(and_1_out), .Clr(1'b0), .Q(Q0), .nQ(nQ0));
endmodule
