// Digital circuit latch-transp-2bits.dig as structural Verilog
module latch_transp_2bits (
  input  EN,
  input  D1,
  input  D0,
  output Q1,
  output Q0
);

  wire and_1_out, and_2_out, and_3_out, and_4_out, and_5_out, and_6_out, not_1_out, not_2_out, or_1_out,
       or_2_out, or_3_out, or_4_out;

  not not_1 (not_1_out, EN);
  not not_2 (not_2_out, not_1_out);
  and and_1 (and_1_out, Q1, not_1_out);
  and and_2 (and_2_out, Q1, D1);
  and and_3 (and_3_out, not_2_out, D1);
  and and_4 (and_4_out, Q0, not_1_out);
  and and_5 (and_5_out, Q0, D0);
  and and_6 (and_6_out, not_2_out, D0);
  or or_1 (or_1_out, and_2_out, and_3_out);
  or or_2 (or_2_out, and_5_out, and_6_out);
  or or_3 (or_3_out, and_1_out, or_1_out);
  or or_4 (or_4_out, and_4_out, or_2_out);
  and and_7 (Q1, 1'b1, or_3_out);
  and and_8 (Q0, 1'b1, or_4_out);

  // Notes on the sheet:
  //   Q1: pin 5
  //   EN: pin 3
  //   D1: pin 1
  //   Q0: pin 7
  //   D0: pin 2
endmodule
