// Digital circuit latch.dig as structural Verilog
module latch (
  input  EN,
  input  D1,
  input  D0,
  output Q1,
  output Q0
);

  latch_transp_2bits latch_transp_2bits_1 (.EN(EN), .D1(D1), .D0(D0), .Q1(Q1), .Q0(Q0));

  // Notes on the sheet:
  //   EN: default 1
endmodule
