// Digital circuit combinatorio-ac-ou-bc#ne.dig as structural Verilog
module combinatorio_ac_ou_bc_ne (
  input  A,
  input  B,
  input  C,
  output S
);

  wire nand_1_out, nand_2_out;

  nand nand_1 (nand_1_out, A, C);
  nand nand_2 (nand_2_out, C, B);
  nand nand_3 (S, nand_1_out, nand_2_out);
endmodule
