// Digital circuit combinatorio-ac-ou-bc#nou-economico.dig as structural Verilog
module combinatorio_ac_ou_bc_nou_economico (
  input  A,
  input  B,
  input  C,
  output S
);

  wire nor_1_out, nor_2_out;

  nor nor_1 (nor_1_out, A, B);
  nor nor_2 (nor_2_out, C, C);
  nor nor_3 (S, nor_1_out, nor_2_out);
endmodule
