// Digital circuit combinatorio-ac-ou-bc#nou.dig as structural Verilog
module combinatorio_ac_ou_bc_nou (
  input  A,
  input  B,
  input  C,
  output S
);

  wire nor_1_out, nor_2_out, nor_3_out, nor_4_out, nor_5_out, nor_6_out;

  nor nor_1 (nor_1_out, A, A);
  nor nor_2 (nor_2_out, B, B);
  nor nor_3 (nor_3_out, C, C);
  nor nor_4 (nor_4_out, nor_1_out, nor_3_out);
  nor nor_5 (nor_5_out, nor_2_out, nor_3_out);
  nor nor_6 (nor_6_out, nor_4_out, nor_5_out);
  nor nor_7 (S, nor_6_out, nor_6_out);
endmodule
