// Digital circuit contador-assincrono-decrescente-12-a-2-completo.dig as structural Verilog
module contador_assincrono_decrescente_12_a_2_completo (
  input  ck,
  input  POR,
  output Q0,
  output Q1,
  output Q2,
  output Q3
);

  wire and_1_out, jk_ff_as_1_nq, jk_ff_as_2_nq, jk_ff_as_3_nq, or_1_out;

  and and_1 (and_1_out, ~Q3, ~Q2, ~Q1, Q0);  // And
  JK_FF_AS jk_ff_as_1 (.Set(1'b0), .J(1'b1), .C(~ck), .K(1'b1), .Clr(or_1_out), .Q(Q0), .nQ(jk_ff_as_1_nq));
  JK_FF_AS jk_ff_as_2 (.Set(1'b0), .J(1'b1), .C(~jk_ff_as_1_nq), .K(1'b1), .Clr(or_1_out), .Q(Q1), .nQ(jk_ff_as_2_nq));
  or or_1 (or_1_out, POR, and_1_out);
  JK_FF_AS jk_ff_as_3 (.Set(or_1_out), .J(1'b1), .C(~jk_ff_as_2_nq), .K(1'b1), .Clr(1'b0), .Q(Q2), .nQ(jk_ff_as_3_nq));
  JK_FF_AS jk_ff_as_4 (.Set(or_1_out), .J(1'b1), .C(~jk_ff_as_3_nq), .K(1'b1), .Clr(1'b0), .Q(Q3));  // open: nQ
endmodule
