// Digital circuit contador-assincrono-decrescente-12-a-2.dig as structural Verilog
module contador_assincrono_decrescente_12_a_2 (
  input  ck,
  input  POR,
  output Q0,
  output Q1,
  output Q2,
  output Q3
);

  JK_FF_AS jk_ff_as_1 (.Q(Q0));  // open: Set, J, C, K, Clr, nQ
  JK_FF_AS jk_ff_as_2 (.Q(Q1));  // open: Set, J, C, K, Clr, nQ
  JK_FF_AS jk_ff_as_3 (.Q(Q2));  // open: Set, J, C, K, Clr, nQ
  JK_FF_AS jk_ff_as_4 (.Q(Q3));  // open: Set, J, C, K, Clr, nQ
endmodule
