// Digital circuit contador-assincrono-decrescente.dig as structural Verilog
module contador_assincrono_decrescente (
  input  ck,
  input  POR,
  output Q0,
  output Q1,
  output Q2,
  output Q3
);

  wire and_1_out, or_1_out;

  and and_1 (and_1_out, Q3, ~Q2, Q1, Q0);  // And
  JK_FF_AS jk_ff_as_1 (.Set(or_1_out), .J(1'b1), .C(ck), .K(1'b1), .Clr(1'b0), .Q(Q0));  // open: nQ
  or or_1 (or_1_out, POR, and_1_out);
  JK_FF_AS jk_ff_as_2 (.Set(1'b0), .J(1'b1), .C(Q0), .K(1'b1), .Clr(or_1_out), .Q(Q1));  // open: nQ
  JK_FF_AS jk_ff_as_3 (.Set(or_1_out), .J(1'b1), .C(Q1), .K(1'b1), .Clr(1'b0), .Q(Q2));  // open: nQ
  JK_FF_AS jk_ff_as_4 (.Set(1'b0), .J(1'b1), .C(Q2), .K(1'b1), .Clr(or_1_out), .Q(Q3));  // open: nQ
endmodule
