// Digital circuit contador-sincrono-5-1-6-3.dig as structural Verilog
module contador_sincrono_5_1_6_3 (
  input  clk,
  input  POR,
  output Q0,
  output Q1,
  output Q2
);

  wire and_1_out, jk_ff_as_1_nq, jk_ff_as_2_nq;

  JK_FF_AS jk_ff_as_1 (.Set(POR), .J(1'b1), .C(clk), .K(1'b1), .Clr(1'b0), .Q(Q2), .nQ(jk_ff_as_1_nq));
  JK_FF_AS jk_ff_as_2 (
    .Set(1'b0), .J(jk_ff_as_1_nq), .C(clk), .K(jk_ff_as_1_nq), .Clr(POR), .Q(Q1), .nQ(jk_ff_as_2_nq));
  and and_1 (and_1_out, jk_ff_as_2_nq, jk_ff_as_1_nq);
  JK_FF_AS jk_ff_as_3 (.Set(POR), .J(1'b1), .C(clk), .K(and_1_out), .Clr(1'b0), .Q(Q0));  // open: nQ
endmodule
