// Digital circuit esboco-de-contador-com-por.dig as structural Verilog
module esboco_de_contador_com_por (
  input  POR
);

  JK_FF_AS jk_ff_as_1 (.Set(POR), .Clr(1'b0));  // open: J, C, K, Q, nQ
  JK_FF_AS jk_ff_as_2 (.Set(POR), .Clr(1'b0));  // open: J, C, K, Q, nQ
  JK_FF_AS jk_ff_as_3 (.Set(POR), .Clr(1'b0));  // open: J, C, K, Q, nQ
endmodule
