// Digital circuit implementacao-de-funcao-4x2.dig as structural Verilog
module implementacao_de_funcao_4x2 (
  input  A,
  input  B,
  input  C,
  input  D,
  output X,
  output Y
);

  wire nand_1_out, nand_2_out, nand_3_out, nand_4_out, nand_5_out, nand_6_out, nand_7_out, nand_8_out,
       nand_9_out, nand_10_out, nand_11_out, nand_12_out, nand_13_out, nand_14_out, nand_15_out, nand_17_out,
       nand_18_out;

  nand nand_1 (nand_1_out, A, B);
  nand nand_2 (nand_2_out, C, D);
  nand nand_3 (nand_3_out, A, A);
  nand nand_4 (nand_4_out, B, B);
  nand nand_5 (nand_5_out, C, C);
  nand nand_6 (nand_6_out, nand_1_out, nand_1_out);
  nand nand_7 (nand_7_out, nand_2_out, nand_3_out);
  nand nand_8 (nand_8_out, nand_3_out, nand_4_out);
  nand nand_9 (nand_9_out, nand_6_out, D);
  nand nand_10 (nand_10_out, nand_7_out, nand_7_out);
  nand nand_11 (nand_11_out, nand_8_out, nand_8_out);
  nand nand_12 (nand_12_out, nand_9_out, nand_9_out);
  nand nand_13 (nand_13_out, nand_11_out, nand_5_out);
  nand nand_14 (nand_14_out, nand_12_out, nand_10_out);
  nand nand_15 (nand_15_out, nand_13_out, nand_13_out);
  nand nand_16 (X, nand_14_out, nand_14_out);
  nand nand_17 (nand_17_out, nand_9_out, nand_15_out);
  nand nand_18 (nand_18_out, nand_10_out, nand_17_out);
  nand nand_19 (Y, nand_18_out, nand_18_out);

  // Notes on the sheet:
  //   ~AB
  //   ~CD
  //   ~A
  //   ~B
  //   ~C
  //   ____
  //   ~A~CD
  //   ___
  //   AB
  //   ~A~B
  //   ~ABD
  //   ABD
  //   ~A~B~C
  //   _________
  //   ~A~B~C ~ABD
  //   _______________
  //   ~A~B~C ~ABD ~A~CD
endmodule
