// Digital circuit logica-combinatoria.dig as structural Verilog
module logica_combinatoria (
  input  A,
  input  B,
  input  C
);

  wire and_1_out, nand_1_out, or_1_out, xnor_1_out, xor_1_out;

  xnor xnor_1 (xnor_1_out, A, C);
  and and_1 (and_1_out, B, A);
  nand nand_1 (nand_1_out, and_1_out, C);
  or or_1 (or_1_out, and_1_out, C);
  xor xor_1 (xor_1_out, xnor_1_out, nand_1_out, or_1_out);
  LED S (.in(xor_1_out));
endmodule
