// Logisim project 2019_dg_p1.circ as structural Verilog: 2 circuits, main circuit main
module main (
);

  wire A_out, B_out, C_out, nand_1_out, not_1_out, xor_1_out;

  Button A (.out(A_out));
  Button B (.out(B_out));
  Button C (.out(C_out));
  not not_1 (not_1_out, A_out);
  xor xor_1 (xor_1_out, not_1_out, B_out);
  nand nand_1 (nand_1_out, xor_1_out, C_out);
  LED S (.in(nand_1_out));
endmodule

module CircuitoDeExpressaoLogica (
);

  wire and_1_out, and_2_out, and_3_out, nand_1_out, nor_1_out, nor_2_out, nor_3_out, not_1_out, or_1_out,
       undriven, undriven_2, undriven_3, undriven_4, xnor_1_out, xor_1_out;

  and and_1 (and_1_out, undriven, undriven_2);
  and and_2 (and_2_out, undriven_3, undriven_4);
  not not_1 (not_1_out, undriven);
  or or_1 (or_1_out, undriven, undriven_2);
  nand nand_1 (nand_1_out, and_1_out, undriven_4);
  nor nor_1 (nor_1_out, or_1_out, undriven_3);
  nor nor_2 (nor_2_out, nand_1_out, and_2_out);
  and and_3 (and_3_out, nand_1_out, nor_1_out);
  xnor xnor_1 (xnor_1_out, and_2_out, undriven);
  xor xor_1 (xor_1_out, nor_2_out, not_1_out);
  nor nor_3 (nor_3_out, and_3_out, xnor_1_out);

  // Notes on the sheet:
  //   A
  //   B
  //   C
  //   D
  //   X
  //   Y
endmodule
