// Logisim project blocos_digitais_para_prova.circ as structural Verilog: 60 circuits, main circuit MUX_4_1_3767bba4
module MUX_4_1_3767bba4 (
  input  in_1,
  input  in_2,
  input  in_3,
  input  in_4,
  input  in_5,
  input  in_6,
  output out_7
);

  Multiplexer #(.select(2), .enable("false")) multiplexer_1 (
    .in0(in_1), .in1(in_2), .in2(in_3), .in3(in_4), .out(out_7), .sel({in_6, in_5}));
endmodule

module MUX_8_1_9f7c8bec (
  input  in_1,
  input  in_2,
  input  in_3,
  input  in_4,
  input  in_5,
  input  in_6,
  input  in_7,
  input  in_8,
  input  in_9,
  input  in_10,
  input  in_11,
  output out_12
);

  Multiplexer #(.select(3), .enable("false")) multiplexer_1 (
    .in0(in_1), .in1(in_2), .in2(in_3), .in3(in_4), .in4(in_5), .in5(in_6), .in6(in_7), .in7(in_8),
    .out(out_12), .sel({in_11, in_10, in_9}));
endmodule

module Flip_Flop_RS_NOU_0e20ed83 (
  input  R,
  input  S,
  output Q,
  output Qn
);

  nor nor_1 (Q, R, Qn);
  nor nor_2 (Qn, Q, S);
endmodule

module Flip_Flop_JK_ck1_clr1 (
  input  in_1,
  input  in_2,
  input  in_3,
  input  in_4,
  input  in_5,
  output out_6,
  output out_7
);

  J_K_Flip_Flop j_k_ff_1 (.J(in_2), .K(in_3), .clk(in_4), .Q(out_6), .Qn(out_7), .preset(in_1), .reset(in_5));
endmodule

module Flip_Flop_JK_ck0_clr1 (
  input  in_1,
  input  in_2,
  input  in_3,
  input  in_4,
  input  in_5,
  output out_6,
  output out_7
);

  wire not_1_out;

  J_K_Flip_Flop j_k_ff_1 (.J(in_2), .K(in_3), .clk(not_1_out), .Q(out_6), .Qn(out_7), .preset(in_1), .reset(in_5));
  not not_1 (not_1_out, in_4);
endmodule

module Flip_Flop_D_9b98735a (
  input  in_1,
  input  in_2,
  input  in_3,
  input  in_4,
  output out_5,
  output out_6
);

  D_Flip_Flop d_ff_1 (.clk(in_1), .D(in_2), .Q(out_5), .Qn(out_6), .preset(in_3), .reset(in_4));
endmodule

module Flip_Flop_D_ck1_clr1_dda0a08a (
  input  in_1,
  input  in_2,
  input  in_3,
  output out_4,
  output out_5
);

  D_Flip_Flop d_ff_1 (.clk(in_1), .D(in_2), .Q(out_4), .Qn(out_5), .reset(in_3));  // open: preset
endmodule

module Flip_Flop_D_ck0_clr1_2f9e41fa (
  input  in_1,
  input  in_2,
  input  in_3,
  output out_4,
  output out_5
);

  D_Flip_Flop #(.trigger("falling")) d_ff_1 (
    .clk(in_1), .D(in_2), .Q(out_4), .Qn(out_5), .reset(in_3));  // open: preset
endmodule

module Flip_Flop_D_ck0_pre0_clr0_7318f85d (
  input  in_1,
  input  in_2,
  input  in_3,
  input  in_4,
  output out_5,
  output out_6
);

  wire not_1_out, not_2_out;

  D_Flip_Flop #(.trigger("falling")) d_ff_1 (
    .clk(in_1), .D(in_2), .Q(out_5), .Qn(out_6), .preset(not_2_out), .reset(not_1_out));
  not not_1 (not_1_out, in_4);
  not not_2 (not_2_out, in_3);
endmodule

module Flip_Flip_T_933f9504 (
  input  in_1,
  input  in_2,
  input  in_3,
  input  in_4,
  output out_5,
  output out_6
);

  T_Flip_Flop t_ff_1 (.clk(in_1), .T(in_2), .Q(out_5), .Qn(out_6), .preset(in_3), .reset(in_4));
endmodule

module Flip_Flop_T_ck1_pre0_clr0_56fb84c8 (
  input  in_1,
  input  in_2,
  input  in_3,
  input  in_4,
  output out_5,
  output out_6
);

  wire not_1_out, not_2_out;

  T_Flip_Flop t_ff_1 (.clk(in_1), .T(in_2), .Q(out_5), .Qn(out_6), .preset(not_2_out), .reset(not_1_out));
  not not_1 (not_1_out, in_4);
  not not_2 (not_2_out, in_3);
endmodule

module Express_o_MUX_ETE101_D_2013_P3_Q1_de90289a (
);

  wire mux_8_1_9f7c8bec_1_out_12, undriven, undriven_2, undriven_3;

  MUX_8_1_9f7c8bec mux_8_1_9f7c8bec_1 (
    .in_1(1'b1), .in_2(1'b0), .in_3(1'b1), .in_4(1'b0), .in_5(1'b0), .in_6(1'b1), .in_7(1'b0), .in_8(1'b1),
    .in_9(undriven_3), .in_10(undriven_2), .in_11(undriven), .out_12(mux_8_1_9f7c8bec_1_out_12));

  // Notes on the sheet:
  //   +Vcc
  //   A
  //   C
  //   B
  //   S
endmodule

module Expressao_MUX_ETE102_N_P1_2015_edf40540 (
);

  wire A_out, B_out, mux_4_1_3767bba4_1_out_7;

  MUX_4_1_3767bba4 mux_4_1_3767bba4_1 (
    .in_1(1'b1), .in_2(1'b0), .in_3(1'b0), .in_4(1'b0), .in_5(B_out), .in_6(A_out),
    .out_7(mux_4_1_3767bba4_1_out_7));
  LED S (.in(mux_4_1_3767bba4_1_out_7));
  Button A (.out(A_out));
  Button B (.out(B_out));
endmodule

module Contador_Johnson_ETE101_D_2013_P3_Q2_535e0706 (
);

  wire CK_out, flip_flop_d_ck1_clr1_dda0a08a_1_out_4, flip_flop_d_ck1_clr1_dda0a08a_2_out_4,
       flip_flop_d_ck1_clr1_dda0a08a_3_out_4, flip_flop_d_ck1_clr1_dda0a08a_3_out_5, POR_out;

  Flip_Flop_D_ck1_clr1_dda0a08a flip_flop_d_ck1_clr1_dda0a08a_1 (
    .in_1(CK_out), .in_2(flip_flop_d_ck1_clr1_dda0a08a_3_out_5),
    .out_4(flip_flop_d_ck1_clr1_dda0a08a_1_out_4), .in_3(POR_out));  // open: out_5
  Button CK (.out(CK_out));
  Button POR (.out(POR_out));
  LED Q1 (.in(flip_flop_d_ck1_clr1_dda0a08a_2_out_4));
  LED Q2 (.in(flip_flop_d_ck1_clr1_dda0a08a_1_out_4));
  Flip_Flop_D_ck1_clr1_dda0a08a flip_flop_d_ck1_clr1_dda0a08a_2 (
    .in_1(CK_out), .in_2(flip_flop_d_ck1_clr1_dda0a08a_1_out_4),
    .out_4(flip_flop_d_ck1_clr1_dda0a08a_2_out_4), .in_3(POR_out));  // open: out_5
  LED Q0 (.in(flip_flop_d_ck1_clr1_dda0a08a_3_out_4));
  Flip_Flop_D_ck1_clr1_dda0a08a flip_flop_d_ck1_clr1_dda0a08a_3 (
    .in_1(CK_out), .in_2(flip_flop_d_ck1_clr1_dda0a08a_2_out_4),
    .out_4(flip_flop_d_ck1_clr1_dda0a08a_3_out_4), .out_5(flip_flop_d_ck1_clr1_dda0a08a_3_out_5),
    .in_3(POR_out));
endmodule

module Carta_de_Tempos_FF_JK_ETE101_D_2013_P3_Q3_5e005416 (
);

  wire flip_flop_jk_ck1_clr1_1_out_6, flip_flop_jk_ck1_clr1_1_out_7, undriven, undriven_2, undriven_3,
       undriven_4, undriven_5;

  Flip_Flop_JK_ck1_clr1 flip_flop_jk_ck1_clr1_1 (
    .in_2(undriven), .in_3(undriven_3), .in_4(undriven_2), .out_6(flip_flop_jk_ck1_clr1_1_out_6),
    .out_7(flip_flop_jk_ck1_clr1_1_out_7), .in_1(undriven_4), .in_5(undriven_5));
endmodule

module Tabela_Verdade_FF_T_ETE101_D_2013_P3_Q4_9661a8bf (
);

  wire flip_flop_t_ck1_pre0_clr0_56fb84c8_1_out_5, flip_flop_t_ck1_pre0_clr0_56fb84c8_1_out_6, undriven,
       undriven_2, undriven_3, undriven_4;

  Flip_Flop_T_ck1_pre0_clr0_56fb84c8 flip_flop_t_ck1_pre0_clr0_56fb84c8_1 (
    .in_1(undriven_2), .in_2(undriven), .out_5(flip_flop_t_ck1_pre0_clr0_56fb84c8_1_out_5),
    .out_6(flip_flop_t_ck1_pre0_clr0_56fb84c8_1_out_6), .in_3(undriven_3), .in_4(undriven_4));
endmodule

module Divisor_de_Frequencia_ETE101_D_2013_P4_Q1a_670480f7 (
);

  wire and_1_out, cke_out, flip_flop_d_ck0_clr1_2f9e41fa_1_out_5, flip_flop_d_ck0_clr1_2f9e41fa_2_out_5,
       flip_flop_d_ck0_clr1_2f9e41fa_3_out_5, Q0, Q1, Q2;

  Clock cke (.out(cke_out));
  and and_1 (and_1_out, Q2, Q1, Q0);
  Flip_Flop_D_ck0_clr1_2f9e41fa flip_flop_d_ck0_clr1_2f9e41fa_1 (
    .in_1(cke_out), .in_2(flip_flop_d_ck0_clr1_2f9e41fa_1_out_5), .out_4(Q0),
    .out_5(flip_flop_d_ck0_clr1_2f9e41fa_1_out_5), .in_3(and_1_out));
  Flip_Flop_D_ck0_clr1_2f9e41fa flip_flop_d_ck0_clr1_2f9e41fa_2 (
    .in_1(Q0), .in_2(flip_flop_d_ck0_clr1_2f9e41fa_2_out_5), .out_4(Q1),
    .out_5(flip_flop_d_ck0_clr1_2f9e41fa_2_out_5), .in_3(and_1_out));
  LED cks (.in(Q2));
  Flip_Flop_D_ck0_clr1_2f9e41fa flip_flop_d_ck0_clr1_2f9e41fa_3 (
    .in_1(Q1), .in_2(flip_flop_d_ck0_clr1_2f9e41fa_3_out_5), .out_4(Q2),
    .out_5(flip_flop_d_ck0_clr1_2f9e41fa_3_out_5), .in_3(and_1_out));
endmodule

module Divisor_de_Frequencia_ETE101_D_2013_P4_Q1b_96ce2bfe (
);

  wire cks, flip_flop_d_ck0_clr1_2f9e41fa_1_out_4, flip_flop_d_ck0_clr1_2f9e41fa_1_out_5;

  LED cks_c960a659 (.in(flip_flop_d_ck0_clr1_2f9e41fa_1_out_4));
  Flip_Flop_D_ck0_clr1_2f9e41fa flip_flop_d_ck0_clr1_2f9e41fa_1 (
    .in_1(cks), .in_2(flip_flop_d_ck0_clr1_2f9e41fa_1_out_5), .out_4(flip_flop_d_ck0_clr1_2f9e41fa_1_out_4),
    .out_5(flip_flop_d_ck0_clr1_2f9e41fa_1_out_5));  // open: in_3
endmodule

module Logica_Combinatoria_XOR_NAND_ETE102_b3914503 (
);

  wire A_out, B_out, C_out, nand_1_out, xor_1_out;

  Button A (.out(A_out));
  Button B (.out(B_out));
  Button C (.out(C_out));
  // XOR_Gate xor_1 has open pins: out=xor_1_out
  nand nand_1 (nand_1_out, xor_1_out, C_out);
  LED S (.in(nand_1_out));
endmodule

module Logica_Realimentada_Contexto_Caixa_DAgua_ETE102_2d090a68 (
);

  wire a_out, and_1_out, b_out, or_1_out;

  Button a (.out(a_out));
  Button b (.out(b_out));
  // AND_Gate and_1 has open pins: out=and_1_out
  buf or_1 (or_1_out, and_1_out);  // OR_Gate
  LED V (.in(or_1_out));

  // Notes on the sheet:
  //   REALIMENTAÇÃO
endmodule

module contador_assincrono_12_a_3_b9a22c0a (
);

  wire and_1_out, clock_1_out, flip_flip_t_933f9504_1_out_5, flip_flip_t_933f9504_2_out_5,
       flip_flip_t_933f9504_3_out_5, flip_flip_t_933f9504_4_out_5, or_1_out, POR_out, undriven, undriven_2,
       undriven_3, undriven_4;

  Clock clock_1 (.out(clock_1_out));
  Button POR (.out(POR_out));
  and and_1 (and_1_out, ~undriven_2, ~undriven_3, undriven, ~undriven_4);  // AND_Gate
  Flip_Flip_T_933f9504 flip_flip_t_933f9504_1 (
    .in_1(clock_1_out), .in_2(1'b1), .out_5(flip_flip_t_933f9504_1_out_5), .in_3(1'b0), .in_4(or_1_out));  // open: out_6
  LED Q0 (.in(flip_flip_t_933f9504_1_out_5));
  or or_1 (or_1_out, POR_out, and_1_out);
  Flip_Flip_T_933f9504 flip_flip_t_933f9504_2 (
    .in_1(flip_flip_t_933f9504_1_out_5), .in_2(1'b1), .out_5(flip_flip_t_933f9504_2_out_5), .in_3(1'b0),
    .in_4(or_1_out));  // open: out_6
  LED Q1 (.in(flip_flip_t_933f9504_2_out_5));
  Flip_Flip_T_933f9504 flip_flip_t_933f9504_3 (
    .in_1(flip_flip_t_933f9504_2_out_5), .in_2(1'b1), .out_5(flip_flip_t_933f9504_3_out_5), .in_3(or_1_out),
    .in_4(1'b0));  // open: out_6
  Flip_Flip_T_933f9504 flip_flip_t_933f9504_4 (
    .in_1(flip_flip_t_933f9504_3_out_5), .in_2(1'b1), .out_5(flip_flip_t_933f9504_4_out_5), .in_3(or_1_out),
    .in_4(1'b0));  // open: out_6
  LED Q2 (.in(flip_flip_t_933f9504_3_out_5));
  LED Q3 (.in(flip_flip_t_933f9504_4_out_5));

  // Notes on the sheet:
  //   Q3
  //   Q2
  //   Q1
  //   Q0
endmodule

module contador_assincrono_11_a_1_bf6823f4 (
);

  wire and_1_out, clock_1_out, flip_flip_t_933f9504_1_out_5, flip_flip_t_933f9504_2_out_5,
       flip_flip_t_933f9504_3_out_5, flip_flip_t_933f9504_4_out_5, or_1_out, POR_out, undriven, undriven_2,
       undriven_3, undriven_4;

  Clock clock_1 (.out(clock_1_out));
  Button POR (.out(POR_out));
  and and_1 (and_1_out, ~undriven, ~undriven_2, ~undriven_3, ~undriven_4);  // AND_Gate
  Flip_Flip_T_933f9504 flip_flip_t_933f9504_1 (
    .in_1(clock_1_out), .in_2(1'b1), .out_5(flip_flip_t_933f9504_1_out_5), .in_3(or_1_out), .in_4(1'b0));  // open: out_6
  LED Q0 (.in(flip_flip_t_933f9504_1_out_5));
  or or_1 (or_1_out, POR_out, and_1_out);
  Flip_Flip_T_933f9504 flip_flip_t_933f9504_2 (
    .in_1(flip_flip_t_933f9504_1_out_5), .in_2(1'b1), .out_5(flip_flip_t_933f9504_2_out_5), .in_3(or_1_out),
    .in_4(1'b0));  // open: out_6
  LED Q1 (.in(flip_flip_t_933f9504_2_out_5));
  Flip_Flip_T_933f9504 flip_flip_t_933f9504_3 (
    .in_1(flip_flip_t_933f9504_2_out_5), .in_2(1'b1), .out_5(flip_flip_t_933f9504_3_out_5), .in_3(1'b0),
    .in_4(or_1_out));  // open: out_6
  Flip_Flip_T_933f9504 flip_flip_t_933f9504_4 (
    .in_1(flip_flip_t_933f9504_3_out_5), .in_2(1'b1), .out_5(flip_flip_t_933f9504_4_out_5), .in_3(or_1_out),
    .in_4(1'b0));  // open: out_6
  LED Q2 (.in(flip_flip_t_933f9504_3_out_5));
  LED Q3 (.in(flip_flip_t_933f9504_4_out_5));

  // Notes on the sheet:
  //   Q3
  //   Q2
  //   Q1
  //   Q0
endmodule

module Circuito_l_gico_01_9fd13e7a (
);

  wire A_out, and_1_out, B_out, C_out, D_out, nand_1_out, not_1_out, or_1_out, xnor_1_out, xor_1_out;

  Button B (.out(B_out));
  Button A (.out(A_out));
  Button C (.out(C_out));
  Button D (.out(D_out));
  xor xor_1 (xor_1_out, A_out, B_out);
  nand nand_1 (nand_1_out, C_out, D_out);
  not not_1 (not_1_out, D_out);
  or or_1 (or_1_out, xor_1_out, nand_1_out);
  xnor xnor_1 (xnor_1_out, not_1_out, B_out);
  and and_1 (and_1_out, or_1_out, xnor_1_out);
  LED S (.in(and_1_out));
endmodule

module Circuito_l_gico_02_67dc9f5c (
);

  wire A_out, and_1_out, B_out, C_out, D_out, E_out, nand_1_out, nor_1_out, or_1_out;

  Button A (.out(A_out));
  Button B (.out(B_out));
  Button C (.out(C_out));
  Button D (.out(D_out));
  Button E (.out(E_out));
  nor nor_1 (nor_1_out, A_out, B_out);
  or or_1 (or_1_out, nor_1_out, nand_1_out);
  nand nand_1 (nand_1_out, C_out, D_out);
  LED S (.in(and_1_out));
  and and_1 (and_1_out, or_1_out, E_out);
endmodule

module Contador_S_ncrono_01_416ac4d3 (
);

  wire clock_1_out, flip_flop_jk_ck1_clr1_1_out_7, flip_flop_jk_ck1_clr1_3_out_7, nand_1_out, nand_2_out,
       nand_3_out, POR_out, Q0, Q1, Q2, xor_1_out;

  Clock clock_1 (.out(clock_1_out));
  Button POR (.out(POR_out));
  xor xor_1 (xor_1_out, Q1, Q0);
  LED u_Q2 (.in(Q2));
  Flip_Flop_JK_ck1_clr1 flip_flop_jk_ck1_clr1_1 (
    .in_2(Q0), .in_3(xor_1_out), .in_4(clock_1_out), .out_6(Q2), .out_7(flip_flop_jk_ck1_clr1_1_out_7),
    .in_5(POR_out));  // open: in_1
  Flip_Flop_JK_ck1_clr1 flip_flop_jk_ck1_clr1_2 (
    .in_2(Q2), .in_3(nand_1_out), .in_4(clock_1_out), .out_6(Q1), .in_1(POR_out));  // open: out_7, in_5
  nand nand_1 (nand_1_out, Q2, flip_flop_jk_ck1_clr1_3_out_7);
  LED u_Q1 (.in(Q1));
  Flip_Flop_JK_ck1_clr1 flip_flop_jk_ck1_clr1_3 (
    .in_2(nand_2_out), .in_3(nand_3_out), .in_4(clock_1_out), .out_6(Q0),
    .out_7(flip_flop_jk_ck1_clr1_3_out_7), .in_1(POR_out));  // open: in_5
  nand nand_2 (nand_2_out, Q1, flip_flop_jk_ck1_clr1_1_out_7);
  nand nand_3 (nand_3_out, Q1, Q2);
  LED u_Q0 (.in(Q0));
endmodule

module Contador_S_ncrono_01_Simplificado_b04b98e5 (
);

  wire clock_1_out, flip_flop_jk_ck1_clr1_1_out_6, flip_flop_jk_ck1_clr1_2_out_6,
       flip_flop_jk_ck1_clr1_3_out_6, nand_2_out, nand_3_out, POR_out, undriven, undriven_2, undriven_3,
       undriven_4, undriven_5, undriven_6, xor_1_out;

  Clock clock_1 (.out(clock_1_out));
  Button POR (.out(POR_out));
  xor xor_1 (xor_1_out, undriven_2, undriven_3);
  LED Q2 (.in(flip_flop_jk_ck1_clr1_1_out_6));
  Flip_Flop_JK_ck1_clr1 flip_flop_jk_ck1_clr1_1 (
    .in_2(undriven), .in_3(xor_1_out), .in_4(clock_1_out), .out_6(flip_flop_jk_ck1_clr1_1_out_6),
    .in_5(POR_out));  // open: out_7, in_1
  nand nand_1 (POR_out, flip_flop_jk_ck1_clr1_1_out_6, undriven_4);
  LED Q1 (.in(flip_flop_jk_ck1_clr1_2_out_6));
  Flip_Flop_JK_ck1_clr1 flip_flop_jk_ck1_clr1_2 (
    .in_2(flip_flop_jk_ck1_clr1_1_out_6), .in_3(POR_out), .in_4(clock_1_out),
    .out_6(flip_flop_jk_ck1_clr1_2_out_6), .in_1(POR_out));  // open: out_7, in_5
  Flip_Flop_JK_ck1_clr1 flip_flop_jk_ck1_clr1_3 (
    .in_2(nand_2_out), .in_3(nand_3_out), .in_4(clock_1_out), .out_6(flip_flop_jk_ck1_clr1_3_out_6),
    .in_1(POR_out));  // open: out_7, in_5
  nand nand_2 (nand_2_out, flip_flop_jk_ck1_clr1_2_out_6, undriven_5);
  nand nand_3 (nand_3_out, flip_flop_jk_ck1_clr1_2_out_6, undriven_6);
  LED Q0 (.in(flip_flop_jk_ck1_clr1_3_out_6));

  // Notes on the sheet:
  //   Q0
  //   Q1
  //   Q0
  //   Q0n
  //   Q2n
  //   Q2
endmodule

module Contador_S_ncrono_02_Incompleto_cd5eb075 (
);

  wire clock_1_out, flip_flop_jk_ck1_clr1_1_out_6, flip_flop_jk_ck1_clr1_1_out_7,
       flip_flop_jk_ck1_clr1_2_out_6, flip_flop_jk_ck1_clr1_2_out_7, flip_flop_jk_ck1_clr1_3_out_6,
       flip_flop_jk_ck1_clr1_3_out_7, POR_out, undriven, undriven_2, undriven_3, undriven_4, undriven_5,
       undriven_6, undriven_7, undriven_8, undriven_9, undriven_10, undriven_11, undriven_12, undriven_13,
       undriven_14, undriven_15;

  Clock clock_1 (.out(clock_1_out));
  Button POR (.out(POR_out));
  LED Q2 (.in(flip_flop_jk_ck1_clr1_1_out_6));
  Flip_Flop_JK_ck1_clr1 flip_flop_jk_ck1_clr1_1 (
    .in_2(undriven), .in_3(undriven_2), .in_4(undriven_3), .out_6(flip_flop_jk_ck1_clr1_1_out_6),
    .out_7(flip_flop_jk_ck1_clr1_1_out_7), .in_1(undriven_4), .in_5(undriven_5));
  LED Q1 (.in(flip_flop_jk_ck1_clr1_2_out_6));
  Flip_Flop_JK_ck1_clr1 flip_flop_jk_ck1_clr1_2 (
    .in_2(undriven_6), .in_3(undriven_7), .in_4(undriven_8), .out_6(flip_flop_jk_ck1_clr1_2_out_6),
    .out_7(flip_flop_jk_ck1_clr1_2_out_7), .in_1(undriven_9), .in_5(undriven_10));
  Flip_Flop_JK_ck1_clr1 flip_flop_jk_ck1_clr1_3 (
    .in_2(undriven_11), .in_3(undriven_12), .in_4(undriven_13), .out_6(flip_flop_jk_ck1_clr1_3_out_6),
    .out_7(flip_flop_jk_ck1_clr1_3_out_7), .in_1(undriven_14), .in_5(undriven_15));
  LED Q0 (.in(flip_flop_jk_ck1_clr1_3_out_6));
endmodule

module Contador_S_ncrono_02_Completado_5e8b5331 (
);

  wire clock_1_out, flip_flop_jk_ck1_clr1_1_out_6, flip_flop_jk_ck1_clr1_1_out_7,
       flip_flop_jk_ck1_clr1_2_out_6, flip_flop_jk_ck1_clr1_3_out_6, nand_1_out, or_1_out, POR_out, undriven,
       undriven_2, undriven_3, undriven_4, undriven_5, xor_1_out;

  Clock clock_1 (.out(clock_1_out));
  Button POR (.out(POR_out));
  or or_1 (or_1_out, undriven, undriven_2);
  LED Q2 (.in(flip_flop_jk_ck1_clr1_1_out_6));
  Flip_Flop_JK_ck1_clr1 flip_flop_jk_ck1_clr1_1 (
    .in_2(or_1_out), .in_3(undriven_3), .in_4(clock_1_out), .out_6(flip_flop_jk_ck1_clr1_1_out_6),
    .out_7(flip_flop_jk_ck1_clr1_1_out_7), .in_1(POR_out));  // open: in_5
  LED Q1 (.in(flip_flop_jk_ck1_clr1_2_out_6));
  Flip_Flop_JK_ck1_clr1 flip_flop_jk_ck1_clr1_2 (
    .in_2(flip_flop_jk_ck1_clr1_1_out_6), .in_3(flip_flop_jk_ck1_clr1_1_out_7), .in_4(clock_1_out),
    .out_6(flip_flop_jk_ck1_clr1_2_out_6), .in_5(POR_out));  // open: out_7, in_1
  xor xor_1 (xor_1_out, undriven_4, undriven_5);
  Flip_Flop_JK_ck1_clr1 flip_flop_jk_ck1_clr1_3 (
    .in_2(xor_1_out), .in_3(nand_1_out), .in_4(clock_1_out), .out_6(flip_flop_jk_ck1_clr1_3_out_6),
    .in_1(POR_out));  // open: out_7, in_5
  nand nand_1 (nand_1_out, flip_flop_jk_ck1_clr1_2_out_6, undriven_5);
  LED Q0 (.in(flip_flop_jk_ck1_clr1_3_out_6));

  // Notes on the sheet:
  //   Q0
  //   Q1
  //   Q0
  //   Q0
  //   Q2
endmodule

module Express_o_MUX_ETE102_N_P1_2016_b7d478e4 (
);

  wire and_1_out, k_out, mux_4_1_3767bba4_1_out_7, not_1_out, or_1_out, w_out, xor_1_out, y_out;

  Button k (.out(k_out));
  Button w (.out(w_out));
  Button y (.out(y_out));
  and and_1 (and_1_out, k_out, w_out);
  not not_1 (not_1_out, y_out);
  MUX_4_1_3767bba4 mux_4_1_3767bba4_1 (
    .in_1(1'b1), .in_2(1'b0), .in_3(1'b1), .in_4(1'b0), .in_5(xor_1_out), .in_6(or_1_out),
    .out_7(mux_4_1_3767bba4_1_out_7));
  or or_1 (or_1_out, and_1_out, not_1_out);
  xor xor_1 (xor_1_out, w_out, y_out);
  LED S (.in(mux_4_1_3767bba4_1_out_7));
endmodule

module Circuito_l_gico_03_ETE102_N_P1_2016_11ba9aaf (
  input  in_1,
  input  in_2,
  input  in_3,
  input  in_4
);

  wire and_1_out, nor_1_out, not_1_out, or_1_out, xnor_1_out, xor_1_out;

  xnor xnor_1 (xnor_1_out, in_1, in_2);
  nor nor_1 (nor_1_out, in_3, in_4);
  not not_1 (not_1_out, in_2);
  or or_1 (or_1_out, xnor_1_out, nor_1_out);
  xor xor_1 (xor_1_out, in_4, not_1_out);
  and and_1 (and_1_out, or_1_out, xor_1_out);
  LED S (.in(and_1_out));
endmodule

module Circuito_l_gico_04_ETE102_N_P1_2016_b4058baf (
);

  wire A_out, B_out, C_out, D_out, nand_1_out, nand_2_out, nand_3_out, nand_4_out, nand_5_out, nand_6_out;

  Button A (.out(A_out));
  Button B (.out(B_out));
  Button C (.out(C_out));
  Button D (.out(D_out));
  nand nand_1 (nand_1_out, A_out, B_out);
  nand nand_2 (nand_2_out, C_out, D_out);
  nand nand_3 (nand_3_out, nand_1_out, D_out);
  nand nand_4 (nand_4_out, nand_3_out, nand_3_out);
  nand nand_5 (nand_5_out, nand_2_out, nand_2_out);
  LED S (.in(nand_6_out));
  nand nand_6 (nand_6_out, nand_4_out, nand_5_out);
endmodule

module Circuito_l_gico_05_ETE102_N_P1E_2016_df10bf2d (
);

  wire A_out, and_1_out, B_out, C_out, D_out, or_1_out, or_2_out, xnor_1_out, xor_1_out;

  Button B (.out(B_out));
  Button A (.out(A_out));
  Button D (.out(D_out));
  Button C (.out(C_out));
  xnor xnor_1 (xnor_1_out, A_out, B_out);
  and and_1 (and_1_out, C_out, D_out);
  or or_1 (or_1_out, xnor_1_out, and_1_out);
  xor xor_1 (xor_1_out, D_out, B_out);
  LED S (.in(or_2_out));
  or or_2 (or_2_out, or_1_out, xor_1_out);
endmodule

module Contador_S_ncrono_03_Primos_Completo_73c35277 (
);

  wire and_1_out, and_2_out, clock_1_out, flip_flop_jk_ck1_clr1_1_out_6, flip_flop_jk_ck1_clr1_1_out_7,
       flip_flop_jk_ck1_clr1_2_out_6, flip_flop_jk_ck1_clr1_2_out_7, flip_flop_jk_ck1_clr1_3_out_6, POR_out,
       undriven, undriven_2, undriven_3, undriven_4;

  Button POR (.out(POR_out));
  and and_1 (and_1_out, undriven, undriven_2);
  Clock clock_1 (.out(clock_1_out));
  LED Q2 (.in(flip_flop_jk_ck1_clr1_1_out_6));
  Flip_Flop_JK_ck1_clr1 flip_flop_jk_ck1_clr1_1 (
    .in_2(and_1_out), .in_3(undriven), .in_4(clock_1_out), .out_6(flip_flop_jk_ck1_clr1_1_out_6),
    .out_7(flip_flop_jk_ck1_clr1_1_out_7), .in_1(POR_out));  // open: in_5
  LED Q1 (.in(flip_flop_jk_ck1_clr1_2_out_6));
  Flip_Flop_JK_ck1_clr1 flip_flop_jk_ck1_clr1_2 (
    .in_2(undriven_3), .in_3(undriven_3), .in_4(clock_1_out), .out_6(flip_flop_jk_ck1_clr1_2_out_6),
    .out_7(flip_flop_jk_ck1_clr1_2_out_7), .in_1(POR_out));  // open: in_5
  and and_2 (and_2_out, flip_flop_jk_ck1_clr1_2_out_7, undriven_4);
  LED Q0 (.in(flip_flop_jk_ck1_clr1_3_out_6));
  Flip_Flop_JK_ck1_clr1 flip_flop_jk_ck1_clr1_3 (
    .in_2(flip_flop_jk_ck1_clr1_2_out_6), .in_3(and_2_out), .in_4(clock_1_out),
    .out_6(flip_flop_jk_ck1_clr1_3_out_6), .in_1(POR_out));  // open: out_7, in_5

  // Notes on the sheet:
  //   Q1
  //   Q0
  //   Q0
  //   Q2n
  //   Q2n
endmodule

module Contador_S_ncrono_03_Primos_Incompleto_c124bee3 (
);

  wire and_1_out, clock_1_out, flip_flop_jk_ck1_clr1_1_out_6, flip_flop_jk_ck1_clr1_2_out_6,
       flip_flop_jk_ck1_clr1_3_out_6, POR_out, undriven, undriven_2, undriven_3, undriven_4, undriven_5,
       undriven_6, undriven_7, undriven_8, undriven_9;

  Button POR (.out(POR_out));
  and and_1 (and_1_out, undriven, undriven_2);
  Clock clock_1 (.out(clock_1_out));
  LED Q2 (.in(flip_flop_jk_ck1_clr1_1_out_6));
  Flip_Flop_JK_ck1_clr1 flip_flop_jk_ck1_clr1_1 (
    .in_2(and_1_out), .in_3(undriven_4), .in_4(undriven_3), .out_6(flip_flop_jk_ck1_clr1_1_out_6));  // open: out_7, in_1, in_5
  LED Q1 (.in(flip_flop_jk_ck1_clr1_2_out_6));
  Flip_Flop_JK_ck1_clr1 flip_flop_jk_ck1_clr1_2 (
    .in_2(undriven_5), .in_3(undriven_5), .in_4(undriven_6), .out_6(flip_flop_jk_ck1_clr1_2_out_6));  // open: out_7, in_1, in_5
  LED Q0 (.in(flip_flop_jk_ck1_clr1_3_out_6));
  Flip_Flop_JK_ck1_clr1 flip_flop_jk_ck1_clr1_3 (
    .in_2(undriven_7), .in_3(undriven_9), .in_4(undriven_8), .out_6(flip_flop_jk_ck1_clr1_3_out_6));  // open: out_7, in_1, in_5
endmodule

module Contador_Ass_ncrono_01_Divisor_24da7b90 (
);

  wire and_1_out, ck_out, flip_flop_d_9b98735a_1_out_6, flip_flop_d_9b98735a_2_out_6,
       flip_flop_d_9b98735a_3_out_6, flip_flop_d_9b98735a_4_out_6, fs, undriven, undriven_2, undriven_3,
       undriven_4;

  Clock ck (.out(ck_out));
  and and_1 (and_1_out, undriven, ~undriven_2, undriven_3, undriven_4);  // AND_Gate
  Flip_Flop_D_9b98735a flip_flop_d_9b98735a_1 (
    .in_1(ck_out), .in_2(flip_flop_d_9b98735a_1_out_6), .out_6(flip_flop_d_9b98735a_1_out_6), .in_4(and_1_out));  // open: out_5, in_3
  Flip_Flop_D_9b98735a flip_flop_d_9b98735a_2 (
    .in_1(flip_flop_d_9b98735a_1_out_6), .in_2(flip_flop_d_9b98735a_2_out_6),
    .out_6(flip_flop_d_9b98735a_2_out_6), .in_3(and_1_out));  // open: out_5, in_4
  Flip_Flop_D_9b98735a flip_flop_d_9b98735a_3 (
    .in_1(flip_flop_d_9b98735a_2_out_6), .in_2(flip_flop_d_9b98735a_3_out_6),
    .out_6(flip_flop_d_9b98735a_3_out_6), .in_4(and_1_out));  // open: out_5, in_3
  Flip_Flop_D_9b98735a flip_flop_d_9b98735a_4 (
    .in_1(flip_flop_d_9b98735a_3_out_6), .in_2(flip_flop_d_9b98735a_4_out_6), .out_5(fs),
    .out_6(flip_flop_d_9b98735a_4_out_6), .in_4(and_1_out));  // open: in_3

  // Notes on the sheet:
  //   Q3
  //   Q2
  //   Q1
  //   Q0
  //   Q0
  //   Q1
  //   (Considerar inativos os PREs e CLRs não conectados.)
  //   Q2
  //   Q3
  //   fs = 12 kHz
endmodule

module Contador_Ass_ncrono_02_Divisor_181f1af4 (
);

  wire and_1_out, ck_out, flip_flop_d_9b98735a_1_out_6, flip_flop_d_9b98735a_2_out_6,
       flip_flop_d_9b98735a_3_out_6, flip_flop_d_9b98735a_4_out_6, fs, undriven, undriven_2, undriven_3,
       undriven_4;

  Clock ck (.out(ck_out));
  and and_1 (and_1_out, undriven, undriven_2, undriven_3, ~undriven_4);  // AND_Gate
  Flip_Flop_D_9b98735a flip_flop_d_9b98735a_1 (
    .in_1(ck_out), .in_2(flip_flop_d_9b98735a_1_out_6), .out_6(flip_flop_d_9b98735a_1_out_6), .in_3(and_1_out));  // open: out_5, in_4
  Flip_Flop_D_9b98735a flip_flop_d_9b98735a_2 (
    .in_1(flip_flop_d_9b98735a_1_out_6), .in_2(flip_flop_d_9b98735a_2_out_6),
    .out_6(flip_flop_d_9b98735a_2_out_6), .in_3(and_1_out));  // open: out_5, in_4
  Flip_Flop_D_9b98735a flip_flop_d_9b98735a_3 (
    .in_1(flip_flop_d_9b98735a_2_out_6), .in_2(flip_flop_d_9b98735a_3_out_6),
    .out_6(flip_flop_d_9b98735a_3_out_6), .in_4(and_1_out));  // open: out_5, in_3
  Flip_Flop_D_9b98735a flip_flop_d_9b98735a_4 (
    .in_1(flip_flop_d_9b98735a_3_out_6), .in_2(flip_flop_d_9b98735a_4_out_6), .out_5(fs),
    .out_6(flip_flop_d_9b98735a_4_out_6), .in_4(and_1_out));  // open: in_3

  // Notes on the sheet:
  //   Q3
  //   Q2
  //   Q1
  //   Q0
  //   Q0
  //   Q1
  //   (Considerar inativos os PREs e CLRs não conectados.)
  //   Q2
  //   Q3
  //   fs = 650 kHz
endmodule

module Contador_S_ncrono_04_Incompleto_327e838f (
);

  wire clock_1_out, flip_flop_jk_ck1_clr1_1_out_6, flip_flop_jk_ck1_clr1_1_out_7,
       flip_flop_jk_ck1_clr1_2_out_6, flip_flop_jk_ck1_clr1_2_out_7, flip_flop_jk_ck1_clr1_3_out_6,
       flip_flop_jk_ck1_clr1_3_out_7, POR_out, undriven, undriven_2, undriven_3, undriven_4, undriven_5,
       undriven_6, undriven_7, undriven_8, undriven_9, undriven_10, undriven_11, undriven_12, undriven_13,
       undriven_14, undriven_15;

  Clock clock_1 (.out(clock_1_out));
  Button POR (.out(POR_out));
  LED Q2 (.in(flip_flop_jk_ck1_clr1_1_out_6));
  Flip_Flop_JK_ck1_clr1 flip_flop_jk_ck1_clr1_1 (
    .in_2(undriven), .in_3(undriven_2), .in_4(undriven_3), .out_6(flip_flop_jk_ck1_clr1_1_out_6),
    .out_7(flip_flop_jk_ck1_clr1_1_out_7), .in_1(undriven_4), .in_5(undriven_5));
  LED Q1 (.in(flip_flop_jk_ck1_clr1_2_out_6));
  Flip_Flop_JK_ck1_clr1 flip_flop_jk_ck1_clr1_2 (
    .in_2(undriven_6), .in_3(undriven_7), .in_4(undriven_8), .out_6(flip_flop_jk_ck1_clr1_2_out_6),
    .out_7(flip_flop_jk_ck1_clr1_2_out_7), .in_1(undriven_9), .in_5(undriven_10));
  Flip_Flop_JK_ck1_clr1 flip_flop_jk_ck1_clr1_3 (
    .in_2(undriven_11), .in_3(undriven_12), .in_4(undriven_13), .out_6(flip_flop_jk_ck1_clr1_3_out_6),
    .out_7(flip_flop_jk_ck1_clr1_3_out_7), .in_1(undriven_14), .in_5(undriven_15));
  LED Q0 (.in(flip_flop_jk_ck1_clr1_3_out_6));
endmodule

module Contador_S_ncrono_04_Completo_4da59994 (
);

  wire clock_1_out, flip_flop_jk_ck1_clr1_1_out_6, flip_flop_jk_ck1_clr1_1_out_7,
       flip_flop_jk_ck1_clr1_2_out_6, flip_flop_jk_ck1_clr1_2_out_7, flip_flop_jk_ck1_clr1_3_out_6,
       flip_flop_jk_ck1_clr1_3_out_7, POR_out, undriven, undriven_2, undriven_3, undriven_4;

  Clock clock_1 (.out(clock_1_out));
  Button POR (.out(POR_out));
  LED Q2 (.in(flip_flop_jk_ck1_clr1_1_out_6));
  Flip_Flop_JK_ck1_clr1 flip_flop_jk_ck1_clr1_1 (
    .in_2(undriven), .in_3(undriven_2), .in_4(clock_1_out), .out_6(flip_flop_jk_ck1_clr1_1_out_6),
    .out_7(flip_flop_jk_ck1_clr1_1_out_7), .in_1(1'b0), .in_5(POR_out));
  Flip_Flop_JK_ck1_clr1 flip_flop_jk_ck1_clr1_2 (
    .in_2(1'b1), .in_3(1'b1), .in_4(clock_1_out), .out_6(flip_flop_jk_ck1_clr1_2_out_6),
    .out_7(flip_flop_jk_ck1_clr1_2_out_7), .in_1(1'b0), .in_5(POR_out));
  LED Q1 (.in(flip_flop_jk_ck1_clr1_2_out_6));
  LED Q0 (.in(flip_flop_jk_ck1_clr1_3_out_6));
  Flip_Flop_JK_ck1_clr1 flip_flop_jk_ck1_clr1_3 (
    .in_2(undriven_3), .in_3(undriven_4), .in_4(clock_1_out), .out_6(flip_flop_jk_ck1_clr1_3_out_6),
    .out_7(flip_flop_jk_ck1_clr1_3_out_7), .in_1(POR_out), .in_5(1'b0));

  // Notes on the sheet:
  //   Q0
  //   Q0n
  //   (ou Q1n)
  //   Q2n
  //   Q1
  //   (ou Q2n)
  //   Q1n
  //   Q1
  //   (ou Q2)
  //   Q0n
endmodule

module Express_o_MUX_ETE102_N_P1_2017_6e887d1b (
);

  wire and_1_out, clock_1_out, clock_2_out, k_out, mux_8_1_9f7c8bec_1_out_12, nand_1_out, nor_1_out,
       not_1_out, w_out, xor_1_out, y_out;

  Button k (.out(k_out));
  and and_1 (and_1_out, k_out, w_out);
  Button w (.out(w_out));
  not not_1 (not_1_out, y_out);
  Button y (.out(y_out));
  Clock clock_1 (.out(clock_1_out));
  Clock clock_2 (.out(clock_2_out));
  xor xor_1 (xor_1_out, and_1_out, not_1_out);
  nand nand_1 (nand_1_out, y_out, w_out);
  nor nor_1 (nor_1_out, w_out, k_out);
  MUX_8_1_9f7c8bec mux_8_1_9f7c8bec_1 (
    .in_1(1'b0), .in_2(1'b1), .in_3(clock_2_out), .in_4(1'b0), .in_5(1'b1), .in_6(1'b1), .in_7(clock_1_out),
    .in_8(1'b0), .in_9(nor_1_out), .in_10(nand_1_out), .in_11(xor_1_out), .out_12(mux_8_1_9f7c8bec_1_out_12));
  LED S (.in(mux_8_1_9f7c8bec_1_out_12));
endmodule

module Circuito_l_gico_06_ETE102_N_P1_2017_52a7b954 (
);

  wire A_out, and_1_out, and_2_out, and_3_out, B_out, C_out, D_out, nand_1_out, nor_1_out, xor_1_out;

  Button B (.out(B_out));
  Button A (.out(A_out));
  Button C (.out(C_out));
  Button D (.out(D_out));
  nand nand_1 (nand_1_out, A_out, B_out);
  and and_1 (and_1_out, D_out, C_out);
  and and_2 (and_2_out, nand_1_out, D_out);
  nor nor_1 (nor_1_out, and_2_out, and_1_out);
  xor xor_1 (xor_1_out, and_1_out, A_out);
  LED S (.in(and_3_out));
  and and_3 (and_3_out, nor_1_out, xor_1_out);
endmodule

module Circuito_l_gico_07_ETE102_N_P1_2017_9e8ec08b (
);

  wire A_out, and_1_out, and_2_out, B_out, C_out, or_1_out;

  Button A (.out(A_out));
  Button B (.out(B_out));
  Button C (.out(C_out));
  and and_1 (and_1_out, A_out, B_out);
  or or_1 (or_1_out, and_2_out, and_1_out);
  and and_2 (and_2_out, or_1_out, ~C_out);  // AND_Gate
  LED S (.in(and_2_out));
endmodule

module Contador_Ass_ncrono_03_Divisor_Completo_ace8d02e (
);

  wire and_1_out, ck_out, flip_flop_d_ck1_clr1_dda0a08a_1_out_5, flip_flop_d_ck1_clr1_dda0a08a_2_out_5,
       flip_flop_d_ck1_clr1_dda0a08a_3_out_5, flip_flop_d_ck1_clr1_dda0a08a_4_out_5, fs, undriven,
       undriven_2, undriven_3, undriven_4;

  Clock ck (.out(ck_out));
  and and_1 (and_1_out, undriven, undriven_2, ~undriven_3, ~undriven_4);  // AND_Gate
  Flip_Flop_D_ck1_clr1_dda0a08a flip_flop_d_ck1_clr1_dda0a08a_1 (
    .in_1(ck_out), .in_2(flip_flop_d_ck1_clr1_dda0a08a_1_out_5),
    .out_5(flip_flop_d_ck1_clr1_dda0a08a_1_out_5), .in_3(and_1_out));  // open: out_4
  Flip_Flop_D_ck1_clr1_dda0a08a flip_flop_d_ck1_clr1_dda0a08a_2 (
    .in_1(flip_flop_d_ck1_clr1_dda0a08a_1_out_5), .in_2(flip_flop_d_ck1_clr1_dda0a08a_2_out_5),
    .out_5(flip_flop_d_ck1_clr1_dda0a08a_2_out_5), .in_3(and_1_out));  // open: out_4
  Flip_Flop_D_ck1_clr1_dda0a08a flip_flop_d_ck1_clr1_dda0a08a_3 (
    .in_1(flip_flop_d_ck1_clr1_dda0a08a_2_out_5), .in_2(flip_flop_d_ck1_clr1_dda0a08a_3_out_5),
    .out_5(flip_flop_d_ck1_clr1_dda0a08a_3_out_5), .in_3(and_1_out));  // open: out_4
  Flip_Flop_D_ck1_clr1_dda0a08a flip_flop_d_ck1_clr1_dda0a08a_4 (
    .in_1(flip_flop_d_ck1_clr1_dda0a08a_3_out_5), .in_2(flip_flop_d_ck1_clr1_dda0a08a_4_out_5), .out_4(fs),
    .out_5(flip_flop_d_ck1_clr1_dda0a08a_4_out_5), .in_3(and_1_out));

  // Notes on the sheet:
  //   Q3
  //   Q2
  //   Q1
  //   Q0
  //   Q0
  //   Q1
  //   (Considerar inativos os PREs não conectados.)
  //   Q3
  //   Q2
endmodule

module Contador_Ass_ncrono_03_Divisor_Incompleto_932a04ac (
);

  wire ck_out, flip_flop_d_ck1_clr1_dda0a08a_1_out_5, flip_flop_d_ck1_clr1_dda0a08a_2_out_5,
       flip_flop_d_ck1_clr1_dda0a08a_3_out_5, flip_flop_d_ck1_clr1_dda0a08a_4_out_5, fs, undriven;

  Clock ck (.out(ck_out));
  Flip_Flop_D_ck1_clr1_dda0a08a flip_flop_d_ck1_clr1_dda0a08a_1 (
    .in_1(ck_out), .in_2(flip_flop_d_ck1_clr1_dda0a08a_1_out_5),
    .out_5(flip_flop_d_ck1_clr1_dda0a08a_1_out_5), .in_3(undriven));  // open: out_4
  Flip_Flop_D_ck1_clr1_dda0a08a flip_flop_d_ck1_clr1_dda0a08a_2 (
    .in_1(flip_flop_d_ck1_clr1_dda0a08a_1_out_5), .in_2(flip_flop_d_ck1_clr1_dda0a08a_2_out_5),
    .out_5(flip_flop_d_ck1_clr1_dda0a08a_2_out_5), .in_3(undriven));  // open: out_4
  Flip_Flop_D_ck1_clr1_dda0a08a flip_flop_d_ck1_clr1_dda0a08a_3 (
    .in_1(flip_flop_d_ck1_clr1_dda0a08a_2_out_5), .in_2(flip_flop_d_ck1_clr1_dda0a08a_3_out_5),
    .out_5(flip_flop_d_ck1_clr1_dda0a08a_3_out_5), .in_3(undriven));  // open: out_4
  Flip_Flop_D_ck1_clr1_dda0a08a flip_flop_d_ck1_clr1_dda0a08a_4 (
    .in_1(flip_flop_d_ck1_clr1_dda0a08a_3_out_5), .in_2(flip_flop_d_ck1_clr1_dda0a08a_4_out_5), .out_4(fs),
    .out_5(flip_flop_d_ck1_clr1_dda0a08a_4_out_5), .in_3(undriven));

  // Notes on the sheet:
  //   Q0
  //   Q1
  //   (Considerar inativos os PREs não conectados.)
  //   Q2
  //   Q3
endmodule

module Contador_S_ncrono_Johnson_Incompleto_0f052abe (
);

  wire clock_1_out, flip_flop_jk_ck1_clr1_1_p3, flip_flop_jk_ck1_clr1_1_p4, flip_flop_jk_ck1_clr1_1_p5,
       flip_flop_jk_ck1_clr1_2_out_6, flip_flop_jk_ck1_clr1_3_out_6, POR_out, undriven, undriven_2,
       undriven_3, undriven_4, undriven_5, undriven_6;

  Button POR (.out(POR_out));
  Clock clock_1 (.out(clock_1_out));
  LED Q2 (.in(flip_flop_jk_ck1_clr1_1_p5));
  // Flip_Flop_JK_ck1_clr1 flip_flop_jk_ck1_clr1_1: pin names not known; wires that end beside it: POR_out, clock_1_out, flip_flop_jk_ck1_clr1_1_p3, flip_flop_jk_ck1_clr1_1_p4, flip_flop_jk_ck1_clr1_1_p5
  LED Q1 (.in(flip_flop_jk_ck1_clr1_2_out_6));
  Flip_Flop_JK_ck1_clr1 flip_flop_jk_ck1_clr1_2 (
    .in_2(undriven), .in_3(undriven_3), .in_4(undriven_2), .out_6(flip_flop_jk_ck1_clr1_2_out_6));  // open: out_7, in_1, in_5
  LED Q0 (.in(flip_flop_jk_ck1_clr1_3_out_6));
  Flip_Flop_JK_ck1_clr1 flip_flop_jk_ck1_clr1_3 (
    .in_2(undriven_4), .in_3(undriven_6), .in_4(undriven_5), .out_6(flip_flop_jk_ck1_clr1_3_out_6));  // open: out_7, in_1, in_5
endmodule

module Contador_S_ncrono_Johnson_Completo_44f5b873 (
);

  wire clock_1_out, flip_flop_jk_ck1_clr1_1_out_6, flip_flop_jk_ck1_clr1_2_out_6,
       flip_flop_jk_ck1_clr1_3_out_6, POR_out, undriven, undriven_2, undriven_3;

  Button POR (.out(POR_out));
  Clock clock_1 (.out(clock_1_out));
  LED Q2 (.in(flip_flop_jk_ck1_clr1_1_out_6));
  Flip_Flop_JK_ck1_clr1 flip_flop_jk_ck1_clr1_1 (
    .in_2(undriven), .in_3(POR_out), .in_4(clock_1_out), .out_6(flip_flop_jk_ck1_clr1_1_out_6), .in_5(POR_out));  // open: out_7, in_1
  LED Q1 (.in(flip_flop_jk_ck1_clr1_2_out_6));
  Flip_Flop_JK_ck1_clr1 flip_flop_jk_ck1_clr1_2 (
    .in_2(undriven_2), .in_3(clock_1_out), .in_4(clock_1_out), .out_6(flip_flop_jk_ck1_clr1_2_out_6),
    .in_5(POR_out));  // open: out_7, in_1
  LED Q0 (.in(flip_flop_jk_ck1_clr1_3_out_6));
  Flip_Flop_JK_ck1_clr1 flip_flop_jk_ck1_clr1_3 (
    .in_2(undriven_3), .in_3(clock_1_out), .in_4(clock_1_out), .out_6(flip_flop_jk_ck1_clr1_3_out_6),
    .in_5(POR_out));  // open: out_7, in_1

  // Notes on the sheet:
  //   Q1
  //   Q1n
  //   Q0
  //   Q0n
  //   Q2n
  //   Q2
endmodule

module Contador_Ass_ncrono_04_Divisor_Completo_cbf9ddee (
);

  wire ck_out, flip_flop_t_ck1_pre0_clr0_56fb84c8_1_out_6, flip_flop_t_ck1_pre0_clr0_56fb84c8_2_out_6,
       flip_flop_t_ck1_pre0_clr0_56fb84c8_3_out_6, fs, nand_1_out, undriven;

  Clock ck (.out(ck_out));
  not nand_1 (nand_1_out, undriven);  // NAND_Gate
  Flip_Flop_T_ck1_pre0_clr0_56fb84c8 flip_flop_t_ck1_pre0_clr0_56fb84c8_1 (
    .in_1(ck_out), .in_2(1'b1), .out_6(flip_flop_t_ck1_pre0_clr0_56fb84c8_1_out_6), .in_3(1'b1),
    .in_4(nand_1_out));  // open: out_5
  Flip_Flop_T_ck1_pre0_clr0_56fb84c8 flip_flop_t_ck1_pre0_clr0_56fb84c8_2 (
    .in_1(flip_flop_t_ck1_pre0_clr0_56fb84c8_1_out_6), .in_2(1'b1),
    .out_6(flip_flop_t_ck1_pre0_clr0_56fb84c8_2_out_6), .in_3(nand_1_out), .in_4(1'b1));  // open: out_5
  Flip_Flop_T_ck1_pre0_clr0_56fb84c8 flip_flop_t_ck1_pre0_clr0_56fb84c8_3 (
    .in_1(flip_flop_t_ck1_pre0_clr0_56fb84c8_2_out_6), .in_2(1'b1),
    .out_6(flip_flop_t_ck1_pre0_clr0_56fb84c8_3_out_6), .in_3(1'b1), .in_4(nand_1_out));  // open: out_5
  Flip_Flop_T_ck1_pre0_clr0_56fb84c8 flip_flop_t_ck1_pre0_clr0_56fb84c8_4 (
    .in_1(flip_flop_t_ck1_pre0_clr0_56fb84c8_3_out_6), .in_2(1'b1), .out_5(fs), .in_3(1'b1), .in_4(nand_1_out));  // open: out_6

  // Notes on the sheet:
  //   Q3
  //   Q2
  //   Q1
  //   Q0
  //   Q0
  //   Q1
  //   (Considerar inativos os PREs e CLRs não conectados.)
  //   Q2
  //   Q3
endmodule

module Contador_Ass_ncrono_04_Divisor_Inompleto_4938228a (
);

  wire ck_out, flip_flop_t_ck1_pre0_clr0_56fb84c8_1_out_6, flip_flop_t_ck1_pre0_clr0_56fb84c8_2_out_6,
       flip_flop_t_ck1_pre0_clr0_56fb84c8_3_out_6, fs;

  Clock ck (.out(ck_out));
  Flip_Flop_T_ck1_pre0_clr0_56fb84c8 flip_flop_t_ck1_pre0_clr0_56fb84c8_1 (
    .in_1(ck_out), .in_2(1'b1), .out_6(flip_flop_t_ck1_pre0_clr0_56fb84c8_1_out_6));  // open: out_5, in_3, in_4
  Flip_Flop_T_ck1_pre0_clr0_56fb84c8 flip_flop_t_ck1_pre0_clr0_56fb84c8_2 (
    .in_1(flip_flop_t_ck1_pre0_clr0_56fb84c8_1_out_6), .in_2(1'b1),
    .out_6(flip_flop_t_ck1_pre0_clr0_56fb84c8_2_out_6));  // open: out_5, in_3, in_4
  Flip_Flop_T_ck1_pre0_clr0_56fb84c8 flip_flop_t_ck1_pre0_clr0_56fb84c8_3 (
    .in_1(flip_flop_t_ck1_pre0_clr0_56fb84c8_2_out_6), .in_2(1'b1),
    .out_6(flip_flop_t_ck1_pre0_clr0_56fb84c8_3_out_6));  // open: out_5, in_3, in_4
  Flip_Flop_T_ck1_pre0_clr0_56fb84c8 flip_flop_t_ck1_pre0_clr0_56fb84c8_4 (
    .in_1(flip_flop_t_ck1_pre0_clr0_56fb84c8_3_out_6), .in_2(1'b1), .out_5(fs));  // open: out_6, in_3, in_4

  // Notes on the sheet:
  //   Q0
  //   Q1
  //   Q2
  //   Q3
endmodule

module Contador_S_ncrono_05_Completo_10d97a37 (
);

  wire clock_1_out, flip_flop_jk_ck1_clr1_1_out_7, POR_out, Q0, Q1, Q2, xnor_1_out;

  Clock clock_1 (.out(clock_1_out));
  Button POR (.out(POR_out));
  Flip_Flop_JK_ck1_clr1 flip_flop_jk_ck1_clr1_1 (
    .in_2(1'b1), .in_3(xnor_1_out), .in_4(clock_1_out), .out_6(Q2), .out_7(flip_flop_jk_ck1_clr1_1_out_7),
    .in_1(POR_out), .in_5(1'b0));
  xnor xnor_1 (xnor_1_out, Q1, Q0);
  LED u_Q2 (.in(Q2));
  LED u_Q1 (.in(Q1));
  Flip_Flop_JK_ck1_clr1 flip_flop_jk_ck1_clr1_2 (
    .in_2(flip_flop_jk_ck1_clr1_1_out_7), .in_3(1'b1), .in_4(clock_1_out), .out_6(Q1), .in_1(1'b0),
    .in_5(POR_out));  // open: out_7
  LED u_Q0 (.in(Q0));
  Flip_Flop_JK_ck1_clr1 flip_flop_jk_ck1_clr1_3 (
    .in_2(1'b1), .in_3(1'b1), .in_4(clock_1_out), .out_6(Q0), .in_1(POR_out), .in_5(1'b0));  // open: out_7
endmodule

module Contador_S_ncrono_05_Sem_LEDs_e9871d74 (
);

  wire clock_1_out, flip_flop_jk_ck1_clr1_1_out_7, POR_out, Q0, Q1, Q2, xnor_1_out;

  Clock clock_1 (.out(clock_1_out));
  Button POR (.out(POR_out));
  Flip_Flop_JK_ck1_clr1 flip_flop_jk_ck1_clr1_1 (
    .in_2(1'b1), .in_3(xnor_1_out), .in_4(clock_1_out), .out_6(Q2), .out_7(flip_flop_jk_ck1_clr1_1_out_7),
    .in_1(POR_out), .in_5(1'b0));
  xnor xnor_1 (xnor_1_out, Q1, Q0);
  Flip_Flop_JK_ck1_clr1 flip_flop_jk_ck1_clr1_2 (
    .in_2(flip_flop_jk_ck1_clr1_1_out_7), .in_3(1'b1), .in_4(clock_1_out), .out_6(Q1), .in_1(1'b0),
    .in_5(POR_out));  // open: out_7
  Flip_Flop_JK_ck1_clr1 flip_flop_jk_ck1_clr1_3 (
    .in_2(1'b1), .in_3(1'b1), .in_4(clock_1_out), .out_6(Q0), .in_1(POR_out), .in_5(1'b0));  // open: out_7
endmodule

module Contador_Ass_ncrono_05_Completo_0906fbbf (
);

  wire and_1_out, clock_1_out, flip_flop_d_ck0_pre0_clr0_7318f85d_1_out_6,
       flip_flop_d_ck0_pre0_clr0_7318f85d_2_out_6, flip_flop_d_ck0_pre0_clr0_7318f85d_3_out_6, nand_1_out,
       not_1_out, POR_out, Q0, Q1, Q2;

  Clock clock_1 (.out(clock_1_out));
  Button POR (.out(POR_out));
  LED led_1 (.in(Q0));
  Flip_Flop_D_ck0_pre0_clr0_7318f85d flip_flop_d_ck0_pre0_clr0_7318f85d_1 (
    .in_1(clock_1_out), .in_2(flip_flop_d_ck0_pre0_clr0_7318f85d_1_out_6), .out_5(Q0),
    .out_6(flip_flop_d_ck0_pre0_clr0_7318f85d_1_out_6), .in_4(1'b1), .in_3(and_1_out));
  not not_1 (not_1_out, POR_out);
  Flip_Flop_D_ck0_pre0_clr0_7318f85d flip_flop_d_ck0_pre0_clr0_7318f85d_2 (
    .in_1(Q0), .in_2(flip_flop_d_ck0_pre0_clr0_7318f85d_2_out_6), .out_5(Q1),
    .out_6(flip_flop_d_ck0_pre0_clr0_7318f85d_2_out_6), .in_4(1'b1), .in_3(and_1_out));
  LED led_2 (.in(Q1));
  nand nand_1 (nand_1_out, Q2, Q1, Q0);
  and and_1 (and_1_out, nand_1_out, not_1_out);
  LED led_3 (.in(Q2));
  Flip_Flop_D_ck0_pre0_clr0_7318f85d flip_flop_d_ck0_pre0_clr0_7318f85d_3 (
    .in_1(Q1), .in_2(flip_flop_d_ck0_pre0_clr0_7318f85d_3_out_6), .out_5(Q2),
    .out_6(flip_flop_d_ck0_pre0_clr0_7318f85d_3_out_6), .in_4(and_1_out), .in_3(1'b1));

  // Notes on the sheet:
  //   FF0
  //   FF1
  //   FF2
endmodule

module Contador_Ass_ncrono_05_Sem_LEDs_PORn_1f39cde1 (
);

  wire and_1_out, clock_1_out, flip_flop_d_ck0_pre0_clr0_7318f85d_1_out_6,
       flip_flop_d_ck0_pre0_clr0_7318f85d_2_out_6, flip_flop_d_ck0_pre0_clr0_7318f85d_3_out_6, nand_1_out,
       PORn_out, Q0, Q1, Q2;

  Clock clock_1 (.out(clock_1_out));
  Button PORn (.out(PORn_out));
  Flip_Flop_D_ck0_pre0_clr0_7318f85d flip_flop_d_ck0_pre0_clr0_7318f85d_1 (
    .in_1(clock_1_out), .in_2(flip_flop_d_ck0_pre0_clr0_7318f85d_1_out_6), .out_5(Q0),
    .out_6(flip_flop_d_ck0_pre0_clr0_7318f85d_1_out_6), .in_4(1'b1), .in_3(and_1_out));
  Flip_Flop_D_ck0_pre0_clr0_7318f85d flip_flop_d_ck0_pre0_clr0_7318f85d_2 (
    .in_1(Q0), .in_2(flip_flop_d_ck0_pre0_clr0_7318f85d_2_out_6), .out_5(Q1),
    .out_6(flip_flop_d_ck0_pre0_clr0_7318f85d_2_out_6), .in_4(1'b1), .in_3(and_1_out));
  and and_1 (and_1_out, nand_1_out, PORn_out);
  nand nand_1 (nand_1_out, Q2, Q1, ~Q0);  // NAND_Gate
  Flip_Flop_D_ck0_pre0_clr0_7318f85d flip_flop_d_ck0_pre0_clr0_7318f85d_3 (
    .in_1(Q1), .in_2(flip_flop_d_ck0_pre0_clr0_7318f85d_3_out_6), .out_5(Q2),
    .out_6(flip_flop_d_ck0_pre0_clr0_7318f85d_3_out_6), .in_4(and_1_out), .in_3(1'b1));

  // Notes on the sheet:
  //   FF0
  //   FF1
  //   FF2
endmodule

module Registrador_de_Deslocamento_01_Completo_08365fb4 (
);

  wire clock_1_out, flip_flop_rs_nou_0e20ed83_1_q, multiplexer_1_out, multiplexer_2_out, multiplexer_3_out,
       POR_out, Q0, Q1, Q2, Q2n;

  Multiplexer #(.enable("false")) multiplexer_1 (
    .in0(Q1), .in1(1'b1), .out(multiplexer_1_out), .sel(flip_flop_rs_nou_0e20ed83_1_q));
  Clock clock_1 (.out(clock_1_out));
  Button POR (.out(POR_out));
  LED L2 (.in(Q2));
  Flip_Flop_D_ck1_clr1_dda0a08a flip_flop_d_ck1_clr1_dda0a08a_1 (
    .in_1(clock_1_out), .in_2(multiplexer_1_out), .out_4(Q2), .out_5(Q2n), .in_3(POR_out));
  Flip_Flop_RS_NOU_0e20ed83 flip_flop_rs_nou_0e20ed83_1 (
    .R(Q0), .S(Q2n), .Q(flip_flop_rs_nou_0e20ed83_1_q));  // open: Qn
  Multiplexer #(.enable("false")) multiplexer_2 (
    .in0(Q0), .in1(Q2), .out(multiplexer_2_out), .sel(flip_flop_rs_nou_0e20ed83_1_q));
  LED L1 (.in(Q1));
  Flip_Flop_D_ck1_clr1_dda0a08a flip_flop_d_ck1_clr1_dda0a08a_2 (
    .in_1(clock_1_out), .in_2(multiplexer_2_out), .out_4(Q1), .in_3(POR_out));  // open: out_5
  Multiplexer #(.enable("false")) multiplexer_3 (
    .in0(1'b0), .in1(Q1), .out(multiplexer_3_out), .sel(flip_flop_rs_nou_0e20ed83_1_q));
  LED L0 (.in(Q0));
  Flip_Flop_D_ck1_clr1_dda0a08a flip_flop_d_ck1_clr1_dda0a08a_3 (
    .in_1(clock_1_out), .in_2(multiplexer_3_out), .out_4(Q0), .in_3(POR_out));  // open: out_5
endmodule

module Contador_Ass_ncrono_06_Completo_6e4e2769 (
);

  wire and_1_out, clock_1_out, flip_flop_d_ck0_pre0_clr0_7318f85d_1_out_6,
       flip_flop_d_ck0_pre0_clr0_7318f85d_2_out_6, flip_flop_d_ck0_pre0_clr0_7318f85d_3_out_6, nand_1_out,
       not_1_out, POR_out, Q0, Q1, Q2;

  Clock clock_1 (.out(clock_1_out));
  Button POR (.out(POR_out));
  LED led_1 (.in(Q0));
  Flip_Flop_D_ck0_pre0_clr0_7318f85d flip_flop_d_ck0_pre0_clr0_7318f85d_1 (
    .in_1(clock_1_out), .in_2(flip_flop_d_ck0_pre0_clr0_7318f85d_1_out_6), .out_5(Q0),
    .out_6(flip_flop_d_ck0_pre0_clr0_7318f85d_1_out_6), .in_4(1'b1), .in_3(and_1_out));
  not not_1 (not_1_out, POR_out);
  Flip_Flop_D_ck0_pre0_clr0_7318f85d flip_flop_d_ck0_pre0_clr0_7318f85d_2 (
    .in_1(flip_flop_d_ck0_pre0_clr0_7318f85d_1_out_6), .in_2(flip_flop_d_ck0_pre0_clr0_7318f85d_2_out_6),
    .out_5(Q1), .out_6(flip_flop_d_ck0_pre0_clr0_7318f85d_2_out_6), .in_4(1'b1), .in_3(and_1_out));
  LED led_2 (.in(Q1));
  nand nand_1 (nand_1_out, Q2, Q1, ~Q0);  // NAND_Gate
  and and_1 (and_1_out, nand_1_out, not_1_out);
  LED led_3 (.in(Q2));
  Flip_Flop_D_ck0_pre0_clr0_7318f85d flip_flop_d_ck0_pre0_clr0_7318f85d_3 (
    .in_1(flip_flop_d_ck0_pre0_clr0_7318f85d_2_out_6), .in_2(flip_flop_d_ck0_pre0_clr0_7318f85d_3_out_6),
    .out_5(Q2), .out_6(flip_flop_d_ck0_pre0_clr0_7318f85d_3_out_6), .in_4(and_1_out), .in_3(1'b1));

  // Notes on the sheet:
  //   FF0
  //   FF1
  //   FF2
endmodule

module Contador_Ass_ncrono_06_Sem_LEDs_PORn_2b439896 (
);

  wire and_1_out, clock_1_out, flip_flop_d_ck0_pre0_clr0_7318f85d_1_out_6,
       flip_flop_d_ck0_pre0_clr0_7318f85d_2_out_6, flip_flop_d_ck0_pre0_clr0_7318f85d_3_out_6, nand_1_out,
       PORn_out, Q0, Q1, Q2;

  Clock clock_1 (.out(clock_1_out));
  Button PORn (.out(PORn_out));
  Flip_Flop_D_ck0_pre0_clr0_7318f85d flip_flop_d_ck0_pre0_clr0_7318f85d_1 (
    .in_1(clock_1_out), .in_2(flip_flop_d_ck0_pre0_clr0_7318f85d_1_out_6), .out_5(Q0),
    .out_6(flip_flop_d_ck0_pre0_clr0_7318f85d_1_out_6), .in_4(1'b1), .in_3(and_1_out));
  Flip_Flop_D_ck0_pre0_clr0_7318f85d flip_flop_d_ck0_pre0_clr0_7318f85d_2 (
    .in_1(flip_flop_d_ck0_pre0_clr0_7318f85d_1_out_6), .in_2(flip_flop_d_ck0_pre0_clr0_7318f85d_2_out_6),
    .out_5(Q1), .out_6(flip_flop_d_ck0_pre0_clr0_7318f85d_2_out_6), .in_4(1'b1), .in_3(and_1_out));
  nand nand_1 (nand_1_out, Q2, Q1, ~Q0);  // NAND_Gate
  and and_1 (and_1_out, nand_1_out, PORn_out);
  Flip_Flop_D_ck0_pre0_clr0_7318f85d flip_flop_d_ck0_pre0_clr0_7318f85d_3 (
    .in_1(flip_flop_d_ck0_pre0_clr0_7318f85d_2_out_6), .in_2(flip_flop_d_ck0_pre0_clr0_7318f85d_3_out_6),
    .out_5(Q2), .out_6(flip_flop_d_ck0_pre0_clr0_7318f85d_3_out_6), .in_4(and_1_out), .in_3(1'b1));

  // Notes on the sheet:
  //   FF0
  //   FF1
  //   FF2
endmodule

module Contador_S_ncrono_06_Completo_89c31306 (
);

  wire clock_1_out, flip_flop_jk_ck1_clr1_2_out_7, or_1_out, POR_out, Q0, Q0n, Q1, Q2;

  or or_1 (or_1_out, Q1, Q0n);
  Flip_Flop_JK_ck1_clr1 flip_flop_jk_ck1_clr1_1 (
    .in_2(or_1_out), .in_3(1'b1), .in_4(clock_1_out), .out_6(Q2), .in_1(1'b0), .in_5(POR_out));  // open: out_7
  Clock clock_1 (.out(clock_1_out));
  Button POR (.out(POR_out));
  LED u_Q2 (.in(Q2));
  LED u_Q1 (.in(Q1));
  Flip_Flop_JK_ck1_clr1 flip_flop_jk_ck1_clr1_2 (
    .in_2(Q0n), .in_3(Q2), .in_4(clock_1_out), .out_6(Q1), .out_7(flip_flop_jk_ck1_clr1_2_out_7),
    .in_1(POR_out), .in_5(1'b0));
  LED u_Q0 (.in(Q0));
  Flip_Flop_JK_ck1_clr1 flip_flop_jk_ck1_clr1_3 (
    .in_2(1'b1), .in_3(flip_flop_jk_ck1_clr1_2_out_7), .in_4(clock_1_out), .out_6(Q0), .out_7(Q0n),
    .in_1(POR_out), .in_5(1'b0));
endmodule

module Contador_S_ncrono_06_Sem_LEDs_ff35facd (
);

  wire clock_1_out, flip_flop_jk_ck1_clr1_2_out_7, or_1_out, POR_out, Q0, Q0n, Q1, Q2;

  Clock clock_1 (.out(clock_1_out));
  Button POR (.out(POR_out));
  Flip_Flop_JK_ck1_clr1 flip_flop_jk_ck1_clr1_1 (
    .in_2(or_1_out), .in_3(1'b1), .in_4(clock_1_out), .out_6(Q2), .in_1(1'b0), .in_5(POR_out));  // open: out_7
  or or_1 (or_1_out, Q1, Q0n);
  Flip_Flop_JK_ck1_clr1 flip_flop_jk_ck1_clr1_2 (
    .in_2(Q0n), .in_3(Q2), .in_4(clock_1_out), .out_6(Q1), .out_7(flip_flop_jk_ck1_clr1_2_out_7),
    .in_1(POR_out), .in_5(1'b0));
  Flip_Flop_JK_ck1_clr1 flip_flop_jk_ck1_clr1_3 (
    .in_2(1'b1), .in_3(flip_flop_jk_ck1_clr1_2_out_7), .in_4(clock_1_out), .out_6(Q0), .out_7(Q0n),
    .in_1(POR_out), .in_5(1'b0));
endmodule

module i2019p2_Contador_Sincrono (
);

  wire and_1_out, and_2_out, and_3_out, clock_1_out, flip_flop_d_9b98735a_1_out_5,
       flip_flop_d_9b98735a_2_out_5, flip_flop_d_9b98735a_3_out_5, POR_out, undriven, undriven_2, undriven_3,
       undriven_4, undriven_5, undriven_6, undriven_7, undriven_8, undriven_9, undriven_10, xor_1_out;

  Button POR (.out(POR_out));
  Clock clock_1 (.out(clock_1_out));
  LED Q2 (.in(flip_flop_d_9b98735a_1_out_5));
  Flip_Flop_D_9b98735a flip_flop_d_9b98735a_1 (
    .in_1(clock_1_out), .in_2(undriven), .out_5(flip_flop_d_9b98735a_1_out_5), .in_3(POR_out));  // open: out_6, in_4
  and and_1 (and_1_out, ~undriven_2, ~undriven_3);  // AND_Gate
  xor xor_1 (xor_1_out, undriven_4, undriven_5);
  and and_2 (and_2_out, undriven_7, ~undriven_8);  // AND_Gate
  LED Q1 (.in(flip_flop_d_9b98735a_2_out_5));
  Flip_Flop_D_9b98735a flip_flop_d_9b98735a_2 (
    .in_1(clock_1_out), .in_2(undriven_9), .out_5(flip_flop_d_9b98735a_2_out_5), .in_3(POR_out));  // open: out_6, in_4
  and and_3 (and_3_out, ~xor_1_out, ~undriven_6);  // AND_Gate
  LED Q0 (.in(flip_flop_d_9b98735a_3_out_5));
  Flip_Flop_D_9b98735a flip_flop_d_9b98735a_3 (
    .in_1(clock_1_out), .in_2(undriven_10), .out_5(flip_flop_d_9b98735a_3_out_5), .in_4(POR_out));  // open: out_6, in_3

  // Notes on the sheet:
  //   D2
  //   Q2
  //   Q0
  //   Q2
  //   Q1
  //   Q0
  //   Q2
  //   Q1
  //   D1
  //   D0
  //   D2
  //   D1
  //   D0
endmodule

module i2019p2_FlipFlop_RS (
);

  wire clock_1_out, flip_flop_jk_ck0_clr1_1_out_6, flip_flop_jk_ck0_clr1_2_out_6, nand_1_out, nand_2_out,
       POR_out, undriven, undriven_2;

  Clock clock_1 (.out(clock_1_out));
  Button POR (.out(POR_out));
  Flip_Flop_JK_ck0_clr1 flip_flop_jk_ck0_clr1_1 (
    .out_6(flip_flop_jk_ck0_clr1_1_out_6), .in_5(POR_out), .in_4(clock_1_out), .in_3(1'b1), .in_2(1'b1));  // open: in_1, out_7
  Flip_Flop_JK_ck0_clr1 flip_flop_jk_ck0_clr1_2 (
    .out_6(flip_flop_jk_ck0_clr1_2_out_6), .in_5(POR_out), .in_4(flip_flop_jk_ck0_clr1_1_out_6), .in_3(1'b1),
    .in_2(1'b1));  // open: in_1, out_7
  nand nand_1 (nand_1_out, undriven, nand_2_out);
  nand nand_2 (nand_2_out, nand_1_out, undriven_2);
  LED S (.in(nand_1_out));
  LED Sn (.in(nand_2_out));

  // Notes on the sheet:
  //   Q0
  //   Q1
  //   Q0
  //   Q1
endmodule

module i2019ps_FlipFlop_RS (
);

  wire button_1_out, clock_1_out, flip_flop_jk_ck1_clr1_1_out_6, flip_flop_jk_ck1_clr1_2_out_6, nand_1_out,
       nand_2_out, undriven, undriven_2;

  Clock clock_1 (.out(clock_1_out));
  Button button_1 (.out(button_1_out));
  Flip_Flop_JK_ck1_clr1 flip_flop_jk_ck1_clr1_1 (
    .in_2(1'b1), .in_3(1'b1), .in_4(clock_1_out), .out_6(flip_flop_jk_ck1_clr1_1_out_6), .in_5(button_1_out));  // open: out_7, in_1
  Flip_Flop_JK_ck1_clr1 flip_flop_jk_ck1_clr1_2 (
    .in_2(1'b1), .in_3(1'b1), .in_4(flip_flop_jk_ck1_clr1_1_out_6), .out_6(flip_flop_jk_ck1_clr1_2_out_6),
    .in_5(button_1_out));  // open: out_7, in_1
  nand nand_1 (nand_1_out, undriven, nand_2_out);
  nand nand_2 (nand_2_out, nand_1_out, undriven_2);
  LED led_1 (.in(nand_1_out));
  LED led_2 (.in(nand_2_out));

  // Notes on the sheet:
  //   Q0
  //   Q1
  //   Q0
  //   Q1
endmodule

module i2019ps_Contador_Sincrono (
);

  wire and_1_out, clock_1_out, flip_flop_jk_ck1_clr1_1_out_6, flip_flop_jk_ck1_clr1_2_out_6,
       flip_flop_jk_ck1_clr1_3_out_6, POR_out, undriven, undriven_2, undriven_3, undriven_4, undriven_5,
       undriven_6, undriven_7, undriven_8;

  Button POR (.out(POR_out));
  Clock clock_1 (.out(clock_1_out));
  LED Q2 (.in(flip_flop_jk_ck1_clr1_1_out_6));
  Flip_Flop_JK_ck1_clr1 flip_flop_jk_ck1_clr1_1 (
    .in_2(undriven), .in_3(undriven_2), .in_4(clock_1_out), .out_6(flip_flop_jk_ck1_clr1_1_out_6),
    .in_5(POR_out));  // open: out_7, in_1
  and and_1 (and_1_out, undriven_3, undriven_4);
  LED Q1 (.in(flip_flop_jk_ck1_clr1_2_out_6));
  Flip_Flop_JK_ck1_clr1 flip_flop_jk_ck1_clr1_2 (
    .in_2(undriven_5), .in_3(undriven_6), .in_4(clock_1_out), .out_6(flip_flop_jk_ck1_clr1_2_out_6),
    .in_1(POR_out));  // open: out_7, in_5
  LED Q0 (.in(flip_flop_jk_ck1_clr1_3_out_6));
  Flip_Flop_JK_ck1_clr1 flip_flop_jk_ck1_clr1_3 (
    .in_2(undriven_7), .in_3(undriven_8), .in_4(clock_1_out), .out_6(flip_flop_jk_ck1_clr1_3_out_6),
    .in_1(POR_out));  // open: out_7, in_5

  // Notes on the sheet:
  //   J2
  //   K2
  //   Q1n
  //   Q0
  //   Q2n
  //   Q0n
  //   Q2n
  //   J1
  //   K1
  //   J0
  //   K0
  //   J2
  //   K2
  //   J1
  //   K1
  //   J0
  //   K0
endmodule
