// Digital circuit cartas-de-tempo.dig as structural Verilog
module cartas_de_tempo (
  input  S,
  input  C,
  output Y,
  output Z,
  output Y_2,
  output Z_2
);

  and and_1 (Y, S, C);
  or or_1 (Z, S, C);

  assign Y_2 = 1'b0;
  assign Z_2 = 1'b0;
endmodule

/* Test case Carta de Tempo #1:
S C	Y Z
0 0 	0 0
1 0 	0 0
0 1 	0 0
1 1 	0 0
0 1 	0 0
0 1 	0 0
0 1 	0 0
1 1 	0 0
1 1 	0 0
0 0 	0 0
1 0 	0 0
1 1 	0 0
1 1 	0 0
*/

/* Test case Carta de Tempo #2:
S C	Y Z
0 1 	0 0
1 1 	0 0
0 1 	0 0
1 1 	0 0
0 1 	0 0
0 0 	0 0
0 0 	0 0
1 0 	0 0
1 0 	0 0
0 0 	0 0
1 0 	0 0
1 0 	0 0
1 1 	0 0
*/

/* Test case Carta de Tempo #3:
S C	Y Z
0 0 	0 0
0 0 	0 0
1 1 	0 0
1 1 	0 0
0 1 	0 0
1 1 	0 0
1 1 	0 0
0 1 	0 0
1 1 	0 0
0 0 	0 0
1 0 	0 0
0 1 	0 0
1 1 	0 0
*/

/* Test case Carta de Tempo #4:
S C	Y Z
1 0 	0 0
1 1 	0 0
0 1 	0 0
1 1 	0 0
1 0 	0 0
0 0 	0 0
0 0 	0 0
1 0 	0 0
1 0 	0 0
0 0 	0 0
1 0 	0 0
1 1 	0 0
1 1 	0 0
*/

/* Test case Carta de Tempo #5:
S C	Y Z
0 0 	0 0
1 0 	0 0
0 0 	0 0
1 0 	0 0
0 0 	0 0
1 0 	0 0
0 1 	0 0
1 1 	0 0
1 1 	0 0
0 1 	0 0
0 1 	0 0
1 1 	0 0
1 0 	0 0
*/

/* Test case Carta de Tempo #6:
S C	Y Z
1 0 	0 0
1 0 	0 0
0 1 	0 0
1 1 	0 0
0 0 	0 0
1 0 	0 0
1 0 	0 0
0 0 	0 0
1 0 	0 0
0 0 	0 0
1 0 	0 0
1 1 	0 0
0 1 	0 0
*/

/* Test case Carta de Tempo #7:
S C	Y Z
0 1 	0 0
1 1 	0 0
0 1 	0 0
0 1 	0 0
0 1 	0 0
1 1 	0 0
0 0 	0 0
1 0 	0 0
1 0 	0 0
1 0 	0 0
1 0 	0 0
0 1 	0 0
1 1 	0 0
*/

/* Test case Carta de Tempo #8:
S C	Y Z
1 0 	0 0
0 0 	0 0
1 1 	0 0
0 1 	0 0
1 0 	0 0
1 0 	0 0
0 1 	0 0
1 1 	0 0
1 0 	0 0
0 0 	0 0
0 0 	0 0
0 1 	0 0
1 1 	0 0
*/
