// Digital circuit Circ#3-S2-ieee.dig as structural Verilog
module Circ_3_S2_ieee (
  input  A3,
  input  A2,
  input  A1,
  input  A0,
  output Y
);

  wire and_1_out, and_2_out, and_3_out, and_4_out, and_5_out, not_1_out, not_2_out, or_1_out, or_2_out;

  not not_1 (not_1_out, A2);
  not not_2 (not_2_out, A0);
  and and_1 (and_1_out, not_2_out, A1);
  and and_2 (and_2_out, A0, A2);
  and and_3 (and_3_out, A0, A3);
  and and_4 (and_4_out, A2, A3);
  and and_5 (and_5_out, and_1_out, not_1_out);
  or or_1 (or_1_out, and_3_out, and_4_out);
  or or_2 (or_2_out, and_5_out, and_2_out);
  or or_3 (Y, or_2_out, or_1_out);
endmodule
