// Digital circuit Circ#4-S2-ieee.dig as structural Verilog
module Circ_4_S2_ieee (
  input  A0,
  input  A1,
  input  A2,
  input  A3,
  output Y
);

  wire and_1_out, and_2_out, and_3_out, not_1_out, not_2_out, not_3_out, or_1_out, or_2_out;

  not not_1 (not_1_out, A0);
  not not_2 (not_2_out, A1);
  not not_3 (not_3_out, A3);
  and and_1 (and_1_out, not_2_out, not_3_out);
  and and_2 (and_2_out, A1, A3);
  and and_3 (and_3_out, A2, not_3_out);
  or or_1 (or_1_out, not_1_out, and_1_out);
  or or_2 (or_2_out, and_2_out, and_3_out);
  or or_3 (Y, or_1_out, or_2_out);
endmodule
