// Digital circuit Circ#8-S2-ieee.dig as structural Verilog
module Circ_8_S2_ieee (
  input  A0,
  input  A2,
  input  A3,
  output Y
);

  wire not_1_out, or_1_out;

  not not_1 (not_1_out, A0);
  or or_1 (or_1_out, not_1_out, A2);
  or or_2 (Y, or_1_out, A3);
endmodule
