// Digital circuit nes-conceituais.dig as structural Verilog
module nes_conceituais (
  input  A,
  input  B,
  input  A_2,
  input  B_2,
  input  C,
  input  A_3,
  input  B_3,
  input  C_2,
  input  A_4,
  input  B_4,
  input  A_5,
  input  B_5,
  input  A_6,
  input  B_6,
  input  A_7
);

  wire and_1_out, nand_1_out, nand_2_out, nand_3_out, nand_4_out, nand_5_out, nor_1_out, not_1_out, or_1_out;

  and and_1 (and_1_out, A_6, B_6);
  or or_1 (or_1_out, A_5, B_5);
  nand nand_1 (nand_1_out, A_4, B_4);
  nor nor_1 (nor_1_out, A, B);
  not not_1 (not_1_out, A_7);
  nand nand_2 (nand_2_out, A_2, B_2, C);
  nand nand_3 (nand_3_out, A_3, B_3);
  LED K (.in(and_1_out));
  LED L (.in(or_1_out));
  LED M (.in(nand_1_out));
  LED N (.in(nor_1_out));
  LED O (.in(not_1_out));
  LED Y (.in(nand_2_out));
  nand nand_4 (nand_4_out, nand_3_out, nand_3_out);
  nand nand_5 (nand_5_out, nand_4_out, C_2);
  LED Y_2 (.in(nand_5_out));
endmodule
