// Logisim project circuitos-combinatorios-simples-diversos.circ as structural Verilog
module Circuito_1 (
);

  wire A_out, and_1_out, B_out, C_out, or_1_out;

  Button A (.out(A_out));
  Button B (.out(B_out));
  Button C (.out(C_out));
  and and_1 (and_1_out, A_out, B_out);
  or or_1 (or_1_out, and_1_out, C_out);
  LED S (.in(or_1_out));
endmodule

module Circuito_2 (
);

  wire A_out, and_1_out, and_2_out, B_out, C_out, D_out, nand_1_out, nor_1_out, not_1_out, not_2_out,
       xnor_1_out, xor_1_out;

  Button A (.out(A_out));
  Button C (.out(C_out));
  Button D (.out(D_out));
  Button B (.out(B_out));
  ExactlyOne xor_1 (.out(xor_1_out), .in1(A_out), .in2(D_out), .in3(B_out));
  not not_1 (not_1_out, C_out);
  and and_1 (and_1_out, A_out, D_out);
  and and_2 (and_2_out, ~B_out, C_out);  // AND_Gate
  nor nor_1 (nor_1_out, xor_1_out, not_1_out);
  nand nand_1 (nand_1_out, and_1_out, ~and_2_out);  // NAND_Gate
  xnor xnor_1 (xnor_1_out, nor_1_out, nand_1_out);
  not not_2 (not_2_out, xnor_1_out);
  LED S (.in(not_2_out));
endmodule
