// Logisim project circuitos-digitais.circ as structural Verilog: 1 circuit, main circuit main
module main (
);

  wire and_1_out, and_2_out, not_1_out, undriven, undriven_2;

  not not_1 (not_1_out, undriven_2);
  and and_1 (and_1_out, undriven_2, undriven);
  and and_2 (and_2_out, not_1_out, undriven);

  // Notes on the sheet:
  //   E
  //   A
  //   Y1
  //   Y0
endmodule
